// Logisim project CS1404_U201414667_甘鹏_alu.circ as structural Verilog: 12 circuits, main circuit ALU
module ALU (
  input  [31:0] X,
  input  [31:0] Y,
  input  [3:0] AluOP,
  output Signed_Overflow,
  output UnSigned_Overflow,
  output Equal,
  output [31:0] Result,
  output [31:0] Result_2
);

  wire bitselector_1_out, carry, comparator_1_lt, comparator_2_lt;
  wire [4:0] bitselector_2_out, bitselector_3_out, bitselector_4_out;
  wire [31:0] getcomple_1_out, multiplexer_2_out, multiplexer_4_out, R0, R1, R2, R3, R4, R5, R7, R8, R9, R10,
       R11, R12, R32, R42, X0, X1, X2, X3, X4, X5, X6, X7, X8, X9, X10, X11, X12, Y0, Y1, Y2, Y3, Y4, Y5, Y6,
       Y7, Y8, Y9, Y10, Y11, Y12;

  // Probe on X
  // Probe on X
  Demultiplexer #(.select(4), .width(32)) demultiplexer_1 (
    .out0(X0), .out1(X1), .out2(X2), .out3(X3), .out4(X4), .out5(X5), .out6(X6), .out7(X7), .out8(X8),
    .out9(X9), .out10(X10), .out11(X11), .out12(X12), .in(X), .sel(AluOP), .en(1'b1));  // open: out13, out14, out15
  Demultiplexer #(.select(4), .width(32)) demultiplexer_2 (
    .out0(Y0), .out1(Y1), .out2(Y2), .out3(Y3), .out4(Y4), .out5(Y5), .out6(Y6), .out7(Y7), .out8(Y8),
    .out9(Y9), .out10(Y10), .out11(Y11), .out12(Y12), .in(Y), .sel(AluOP), .en(1'b1));  // open: out13, out14, out15
  Comparator #(.width(32)) comparator_1 (.a(X11), .b(Y11), .lt(comparator_1_lt));  // open: gt, eq
  // Probe on Y
  // Probe on Y
  BitSelector #(.width(4)) bitselector_1 (.in(AluOP), .out(bitselector_1_out), .sel(2'b01));
  Multiplexer #(.width(32)) multiplexer_1 (.in0({32{1'b0}}), .in1(32'h1), .out(R11), .sel(comparator_1_lt), .en(1'b1));
  Comparator #(.width(32), .mode("unsigned")) comparator_2 (.a(X12), .b(Y12), .lt(comparator_2_lt));  // open: gt, eq
  // Probe on AluOP
  BitSelector #(.width(32), .group(5)) bitselector_2 (.in(Y0), .out(bitselector_2_out), .sel(3'b000));
  BitSelector #(.width(32), .group(5)) bitselector_3 (.in(Y1), .out(bitselector_3_out), .sel(3'b000));
  BitSelector #(.width(32), .group(5)) bitselector_4 (.in(Y2), .out(bitselector_4_out), .sel(3'b000));
  Multiplexer #(.width(32)) multiplexer_2 (
    .in0(X5), .in1(X6), .out(multiplexer_2_out), .sel(bitselector_1_out), .en(1'b1));
  assign R7 = X7 & Y7;  // AND_Gate and_1, 32 bits wide
  assign R8 = X8 | Y8;  // OR_Gate or_1, 32 bits wide
  Multiplexer #(.width(32)) multiplexer_3 (.in0({32{1'b0}}), .in1(32'h1), .out(R12), .sel(comparator_2_lt), .en(1'b1));
  // Probe on Result
  // Probe on Result
  Shifter #(.width(32)) shifter_1 (.in(X0), .\dist (bitselector_2_out), .out(R0));
  Shifter #(.width(32), .shift("ar")) shifter_2 (.in(X1), .\dist (bitselector_3_out), .out(R1));
  Shifter #(.width(32), .shift("lr")) shifter_3 (.in(X2), .\dist (bitselector_4_out), .out(R2));
  Multiplier #(.width(32)) multiplier_1 (.a(X3), .b(Y3), .out(R3), .cout(R32));  // open: cin
  Divider #(.width(32)) divider_1 (.a(X4), .b(Y4), .out(R4), .rem(R42));  // open: upper
  Multiplexer #(.width(32)) multiplexer_4 (
    .in0(Y5), .in1(Y6), .out(multiplexer_4_out), .sel(bitselector_1_out), .en(1'b1));
  GetComple getcomple_1 (.in_1(multiplexer_4_out), .in_2(bitselector_1_out), .out(getcomple_1_out));
  FA_32bit fa_32bit_1 (
    .in_1(bitselector_1_out), .in_2(multiplexer_2_out), .in_3(getcomple_1_out), .S(R5), .Cout(carry),
    .OF(Signed_Overflow));
  xor xor_1 (UnSigned_Overflow, bitselector_1_out, carry);
  assign R9 = X9 ^ Y9;  // XOR_Gate xor_2, 32 bits wide
  assign R10 = ~(X10 | Y10);  // NOR_Gate nor_1, 32 bits wide
  Comparator #(.width(32)) comparator_3 (.a(X), .b(Y), .eq(Equal));  // open: gt, lt
  // Probe on Result_2
  Multiplexer #(.select(4), .width(32)) multiplexer_5 (
    .in0(R0), .in1(R1), .in2(R2), .in3(R3), .in4(R4), .in5(R5), .in6(R5), .in7(R7), .in8(R8), .in9(R9),
    .in10(R10), .in11(R11), .in12(R12), .out(Result), .sel(AluOP), .en(1'b1));  // open: in13, in14, in15
  Multiplexer #(.select(4), .width(32)) multiplexer_6 (
    .in0({32{1'b0}}), .in1({32{1'b0}}), .in2({32{1'b0}}), .in3(R32), .in4(R42), .in5({32{1'b0}}),
    .in6({32{1'b0}}), .in7({32{1'b0}}), .in8({32{1'b0}}), .in9({32{1'b0}}), .in10({32{1'b0}}),
    .in11({32{1'b0}}), .in12({32{1'b0}}), .out(Result_2), .sel(AluOP), .en(1'b1));  // open: in13, in14, in15

  // Other names for the same wires on the sheet: OF = Signed_Overflow; Result2[31:0] = Result_2; S[3:0] = AluOP;
  //   UOF = UnSigned_Overflow

  // Notes on the sheet:
  //   不要改变此引脚区域内容，也不要改变ALU封装形式
  //   输入引脚
  //   请在下方利用上方输入输出引脚的隧道信号构建ALU电路，ctrl+d复制选择部件
  //   华中科技大学计算机学院 计算机组成原理，鸣谢加州大学伯克利CS61C课程
  //   输出引脚
  //   探测区域
endmodule

module \演示电路  (
  input  [31:0] X,
  input  [31:0] Y,
  input  [3:0] ALUOP,
  output Signed_Overflow,
  output Unsigned_overflow,
  output [31:0] Result,
  output [31:0] Result_2,
  output Equal
);

  // Probe on X
  // Probe on X
  ALU alu_1 (
    .AluOP(ALUOP), .X(X), .Equal(Equal), .Result(Result), .Signed_Overflow(Signed_Overflow), .Y(Y),
    .Result_2(Result_2), .UnSigned_Overflow(Unsigned_overflow));
  // Probe on ALUOP
  // Probe on Y
  // Probe on Y
  // Probe on Result
  // Probe on Result
  // Probe on Result_2

  // Notes on the sheet:
  //   ALu电路无需调整位置即可连接在该电路中，并且不能出现蓝色线缆和三态输出
endmodule

module \等差数列  (
  input  [31:0] \数列初始值 ,
  input  [31:0] \等差值 ,
  input  \时钟 ,
  output [31:0] Result
);

  // Probe on \数列初始值 
  // Probe on \数列初始值 
  // Probe on \等差值 
  // Probe on \等差值 
  // Probe on Result
  // Probe on Result

  // Other names for the same wires on the sheet: 数列初值[31:0] = \数列初始值 ; 累加和[31:0] = Result

  // Notes on the sheet:
  //   不要改变此引脚区域内容，也不要改变ALU封装形式
  //   请在下方利用上方输入输出引脚的隧道信号构建等差数列求和电路，ctrl+d复制选择部件
  //   华中科技大学计算机学院 计算机组成原理，鸣谢加州大学伯克利CS61C课程
  //   输出引脚
  //   探测区域
endmodule

module FA_32bit (
  input  in_1,
  input  [31:0] in_2,
  input  [31:0] in_3,
  output [31:0] S,
  output Cout,
  output OF
);

  wire C1, fa_16bit_1_g, fa_16bit_1_p;

  FA_16bit fa_16bit_1 (
    .in_1(in_1), .in_2(in_2[15:0]), .in_3(in_3[15:0]), .S(S[15:0]), .P(fa_16bit_1_p), .G(fa_16bit_1_g));  // open: Cout
  FA_16bit fa_16bit_2 (.in_1(C1), .in_2(in_2[31:16]), .in_3(in_3[31:16]), .S(S[31:16]), .Cout(Cout));  // open: P, G
  OFspill ofspill_1 (.in_1(in_2), .in_2(in_3), .in_3(S), .out(OF));
  _74182 u_74182_1 (
    .in_1(in_1), .out_3(C1), .G4(1'b0), .P4(1'b0), .G3(1'b0), .P3(1'b0), .G2(1'b0), .P2(1'b0),
    .G1(fa_16bit_1_g), .P1(fa_16bit_1_p));  // open: out_4, out_5, out, out_2

  // Other names for the same wires on the sheet: X[31:0] = in_2; Y[31:0] = in_3
endmodule

module FA_16bit (
  input  in_1,
  input  [15:0] in_2,
  input  [15:0] in_3,
  output [15:0] S,
  output Cout,
  output P,
  output G
);

  wire C1, C2, C3, fa_4bit_1_g, fa_4bit_1_p, fa_4bit_2_g, fa_4bit_2_p, fa_4bit_3_g, fa_4bit_3_p, fa_4bit_4_g,
       fa_4bit_4_p;

  FA_4bit fa_4bit_1 (
    .in_1(in_1), .in_2(in_2[3:0]), .in_3(in_3[3:0]), .out(S[3:0]), .P(fa_4bit_1_p), .G(fa_4bit_1_g));  // open: Cout
  FA_4bit fa_4bit_2 (
    .in_1(C1), .in_2(in_2[7:4]), .in_3(in_3[7:4]), .out(S[7:4]), .P(fa_4bit_2_p), .G(fa_4bit_2_g));  // open: Cout
  FA_4bit fa_4bit_3 (
    .in_1(C2), .in_2(in_2[11:8]), .in_3(in_3[11:8]), .out(S[11:8]), .P(fa_4bit_3_p), .G(fa_4bit_3_g));  // open: Cout
  FA_4bit fa_4bit_4 (
    .in_1(C3), .in_2(in_2[15:12]), .in_3(in_3[15:12]), .out(S[15:12]), .Cout(Cout), .P(fa_4bit_4_p),
    .G(fa_4bit_4_g));
  _74182 u_74182_1 (
    .in_1(in_1), .out_4(G), .out_5(P), .out(C3), .out_2(C2), .out_3(C1), .G4(fa_4bit_4_g), .P4(fa_4bit_4_p),
    .G3(fa_4bit_3_g), .P3(fa_4bit_3_p), .G2(fa_4bit_2_g), .P2(fa_4bit_2_p), .G1(fa_4bit_1_g), .P1(fa_4bit_1_p));

  // Other names for the same wires on the sheet: A0[3:0] = in_2[3:0]; A1[3:0] = in_2[7:4]; A2[3:0] = in_2[11:8];
  //   A3[3:0] = in_2[15:12]; B0[3:0] = in_3[3:0]; B1[3:0] = in_3[7:4]; B2[3:0] = in_3[11:8]; B3[3:0] = in_3[15:12]
endmodule

module FA_4bit (
  input  in_1,
  input  [3:0] in_2,
  input  [3:0] in_3,
  output [3:0] out,
  output Cout,
  output P,
  output G
);

  wire pg182_1_out, pg182_1_out_2, pg182_1_out_3;

  PG182 pg182_1 (
    .in_2(in_2), .in_3(in_3), .out(pg182_1_out), .out_2(pg182_1_out_2), .out_3(pg182_1_out_3), .out_4(P),
    .out_5(G), .in_1(in_1));
  FA_1bit fa_1bit_1 (.A(in_2[0]), .B(in_3[0]), .Cin(in_1), .S(out[0]));  // open: Cout
  FA_1bit fa_1bit_2 (.A(in_2[1]), .B(in_3[1]), .Cin(pg182_1_out), .S(out[1]));  // open: Cout
  FA_1bit fa_1bit_3 (.A(in_2[2]), .B(in_3[2]), .Cin(pg182_1_out_2), .S(out[2]));  // open: Cout
  FA_1bit fa_1bit_4 (.A(in_2[3]), .B(in_3[3]), .Cin(pg182_1_out_3), .S(out[3]), .Cout(Cout));

  // Other names for the same wires on the sheet: A0 = in_2[0]; A1 = in_2[1]; A2 = in_2[2]; A3 = in_2[3]; B0 = in_3[0];
  //   B1 = in_3[1]; B2 = in_3[2]; B3 = in_3[3]
endmodule

module FA_1bit (
  input  A,
  input  B,
  input  Cin,
  output S,
  output Cout
);

  wire and_1_out, and_2_out, and_3_out;

  xor xor_1 (S, A, B, Cin);
  and and_1 (and_1_out, A, B);
  and and_2 (and_2_out, A, Cin);
  and and_3 (and_3_out, B, Cin);
  or or_1 (Cout, and_1_out, and_2_out, and_3_out);
endmodule

module PG182 (
  input  in_1,
  input  [3:0] in_2,
  input  [3:0] in_3,
  output out,
  output out_2,
  output out_3,
  output out_4,
  output out_5
);

  wire calpg_1_out, calpg_1_out_2, calpg_2_out, calpg_2_out_2, calpg_3_out, calpg_3_out_2, calpg_4_out,
       calpg_4_out_2;

  CalPG calpg_1 (.in_1(in_2[0]), .in_2(in_3[0]), .out(calpg_1_out), .out_2(calpg_1_out_2));
  CalPG calpg_2 (.in_1(in_2[1]), .in_2(in_3[1]), .out(calpg_2_out), .out_2(calpg_2_out_2));
  CalPG calpg_3 (.in_1(in_2[2]), .in_2(in_3[2]), .out(calpg_3_out), .out_2(calpg_3_out_2));
  CalPG calpg_4 (.in_1(in_2[3]), .in_2(in_3[3]), .out(calpg_4_out), .out_2(calpg_4_out_2));
  _74182 u_74182_1 (
    .in_1(in_1), .out_4(out_5), .out_5(out_4), .out(out_3), .out_2(out_2), .out_3(out), .G4(calpg_4_out),
    .P4(calpg_4_out_2), .G3(calpg_3_out), .P3(calpg_3_out_2), .G2(calpg_2_out), .P2(calpg_2_out_2),
    .G1(calpg_1_out), .P1(calpg_1_out_2));
endmodule

module _74182 (
  input  in_1,
  input  G4,
  input  P4,
  input  G3,
  input  P3,
  input  G2,
  input  P2,
  input  G1,
  input  P1,
  output out,
  output out_2,
  output out_3,
  output out_4,
  output out_5
);

  wire and_1_out, and_2_out, and_3_out, and_5_out, and_6_out, and_7_out, and_8_out, and_9_out, and_10_out;

  ExactlyOne xor_1 (.out(out_4), .in0(G4), .in1(and_2_out), .in2(and_1_out), .in3(and_3_out));
  and and_1 (and_1_out, P4, P3, G2);
  and and_2 (and_2_out, P4, G3);
  and and_3 (and_3_out, P4, P3, P2, G1);
  and and_4 (out_5, P4, P3, P2, P1);
  ExactlyOne xor_2 (.out(out), .in0(G3), .in1(and_5_out), .in2(and_6_out), .in3(and_7_out));
  and and_5 (and_5_out, P3, G2);
  and and_6 (and_6_out, P3, P2, G1);
  and and_7 (and_7_out, P3, P2, P1, in_1);
  ExactlyOne xor_3 (.out(out_2), .in0(G2), .in1(and_8_out), .in2(and_9_out));
  and and_8 (and_8_out, P2, G1);
  and and_9 (and_9_out, P2, P1, in_1);
  xor xor_4 (out_3, G1, and_10_out);
  and and_10 (and_10_out, P1, in_1);
endmodule

module CalPG (
  input  in_1,
  input  in_2,
  output out,
  output out_2
);

  and and_1 (out, in_1, in_2);
  xor xor_1 (out_2, in_1, in_2);
endmodule

module OFspill (
  input  [31:0] in_1,
  input  [31:0] in_2,
  input  [31:0] in_3,
  output out
);

  wire and_1_out, and_2_out, bitselector_1_out, bitselector_2_out, bitselector_3_out, not_1_out, not_2_out,
       not_3_out;

  BitSelector #(.width(32)) bitselector_1 (.in(in_1), .out(bitselector_1_out), .sel({5{1'b1}}));
  not not_1 (not_1_out, bitselector_1_out);
  BitSelector #(.width(32)) bitselector_2 (.in(in_2), .out(bitselector_2_out), .sel({5{1'b1}}));
  not not_2 (not_2_out, bitselector_2_out);
  BitSelector #(.width(32)) bitselector_3 (.in(in_3), .out(bitselector_3_out), .sel({5{1'b1}}));
  not not_3 (not_3_out, bitselector_3_out);
  and and_1 (and_1_out, not_1_out, not_2_out, bitselector_3_out);
  or or_1 (out, and_1_out, and_2_out);
  and and_2 (and_2_out, bitselector_1_out, bitselector_2_out, not_3_out);
endmodule

module GetComple (
  input  [31:0] in_1,
  input  in_2,
  output [31:0] out
);

  wire [31:0] not_1_out;

  assign not_1_out = ~in_1;  // NOT_Gate not_1, 32 bits wide
  Multiplexer #(.width(32)) multiplexer_1 (.in0(in_1), .in1(not_1_out), .out(out), .sel(in_2), .en(1'b1));
endmodule
