// Logisim project CS1404_U201414667_甘鹏_regfile.circ as structural Verilog: 2 circuits, main circuit main
module main (
  input  [4:0] Reg1_num,
  input  [4:0] Reg2,
  input  [4:0] Write_Reg_num,
  input  [31:0] Din,
  input  Write_Enable,
  input  Clock,
  output [31:0] Reg1,
  output [31:0] s0_Value,
  output [31:0] s1_Value,
  output [31:0] s2_Value,
  output [31:0] ra_Value,
  output [31:0] v0_Value,
  output [31:0] a0_Value,
  output [31:0] Reg2_2
);

  wire WE0, WE1, WE2, WE3, WE4, WE5, WE6, WE7, WE8, WE9, WE10, WE11, WE12, WE13, WE14, WE15, WE16, WE17,
       WE18, WE19, WE20, WE21, WE22, WE23, WE24, WE25, WE26, WE27, WE28, WE29, WE30, WE31;
  wire [31:0] r0, r1, r3, r5, r6, r7, r8, r9, r10, r11, r12, r13, r14, r15, r19, r20, r21, r22, r23, r24,
       r25, r26, r27, r28, r29, r30;

  Demultiplexer #(.select(5)) demultiplexer_1 (
    .out0(WE0), .out1(WE1), .out2(WE2), .out3(WE3), .out4(WE4), .out5(WE5), .out6(WE6), .out7(WE7),
    .out8(WE8), .out9(WE9), .out10(WE10), .out11(WE11), .out12(WE12), .out13(WE13), .out14(WE14),
    .out15(WE15), .out16(WE16), .out17(WE17), .out18(WE18), .out19(WE19), .out20(WE20), .out21(WE21),
    .out22(WE22), .out23(WE23), .out24(WE24), .out25(WE25), .out26(WE26), .out27(WE27), .out28(WE28),
    .out29(WE29), .out30(WE30), .out31(WE31), .in(Write_Enable), .sel(Write_Reg_num), .en(1'b1));
  Register #(.width(32)) register_1 (.en(1'b0), .Q(r0), .clr(1'b0));  // open: D, clk
  Register #(.width(32), .trigger("falling")) register_2 (.D(Din), .en(WE4), .Q(a0_Value), .clk(Clock), .clr(1'b0));
  Register #(.width(32), .trigger("falling")) register_3 (.D(Din), .en(WE8), .Q(r8), .clk(Clock), .clr(1'b0));
  Register #(.width(32), .trigger("falling")) register_4 (.D(Din), .en(WE12), .Q(r12), .clk(Clock), .clr(1'b0));
  Register #(.width(32), .trigger("falling")) register_5 (.D(Din), .en(WE16), .Q(s0_Value), .clk(Clock), .clr(1'b0));
  Register #(.width(32), .trigger("falling")) register_6 (.D(Din), .en(WE20), .Q(r20), .clk(Clock), .clr(1'b0));
  Register #(.width(32), .trigger("falling")) register_7 (.D(Din), .en(WE24), .Q(r24), .clk(Clock), .clr(1'b0));
  Register #(.width(32), .trigger("falling")) register_8 (.D(Din), .en(WE28), .Q(r28), .clk(Clock), .clr(1'b0));
  Register #(.width(32), .trigger("falling")) register_9 (.D(Din), .en(WE1), .Q(r1), .clk(Clock), .clr(1'b0));
  Register #(.width(32), .trigger("falling")) register_10 (.D(Din), .en(WE5), .Q(r5), .clk(Clock), .clr(1'b0));
  Register #(.width(32), .trigger("falling")) register_11 (.D(Din), .en(WE9), .Q(r9), .clk(Clock), .clr(1'b0));
  Register #(.width(32), .trigger("falling")) register_12 (.D(Din), .en(WE13), .Q(r13), .clk(Clock), .clr(1'b0));
  Register #(.width(32), .trigger("falling")) register_13 (.D(Din), .en(WE17), .Q(s1_Value), .clk(Clock), .clr(1'b0));
  Register #(.width(32), .trigger("falling")) register_14 (.D(Din), .en(WE21), .Q(r21), .clk(Clock), .clr(1'b0));
  Register #(.width(32), .trigger("falling")) register_15 (.D(Din), .en(WE25), .Q(r25), .clk(Clock), .clr(1'b0));
  Register #(.width(32), .trigger("falling")) register_16 (.D(Din), .en(WE29), .Q(r29), .clk(Clock), .clr(1'b0));
  Register #(.width(32), .trigger("falling")) register_17 (.D(Din), .en(WE2), .Q(v0_Value), .clk(Clock), .clr(1'b0));
  Register #(.width(32), .trigger("falling")) register_18 (.D(Din), .en(WE6), .Q(r6), .clk(Clock), .clr(1'b0));
  Register #(.width(32), .trigger("falling")) register_19 (.D(Din), .en(WE10), .Q(r10), .clk(Clock), .clr(1'b0));
  Register #(.width(32), .trigger("falling")) register_20 (.D(Din), .en(WE14), .Q(r14), .clk(Clock), .clr(1'b0));
  Register #(.width(32), .trigger("falling")) register_21 (.D(Din), .en(WE18), .Q(s2_Value), .clk(Clock), .clr(1'b0));
  Register #(.width(32), .trigger("falling")) register_22 (.D(Din), .en(WE22), .Q(r22), .clk(Clock), .clr(1'b0));
  Register #(.width(32), .trigger("falling")) register_23 (.D(Din), .en(WE26), .Q(r26), .clk(Clock), .clr(1'b0));
  Register #(.width(32), .trigger("falling")) register_24 (.D(Din), .en(WE30), .Q(r30), .clk(Clock), .clr(1'b0));
  Register #(.width(32), .trigger("falling")) register_25 (.D(Din), .en(WE3), .Q(r3), .clk(Clock), .clr(1'b0));
  Register #(.width(32), .trigger("falling")) register_26 (.D(Din), .en(WE7), .Q(r7), .clk(Clock), .clr(1'b0));
  Register #(.width(32), .trigger("falling")) register_27 (.D(Din), .en(WE11), .Q(r11), .clk(Clock), .clr(1'b0));
  Register #(.width(32), .trigger("falling")) register_28 (.D(Din), .en(WE15), .Q(r15), .clk(Clock), .clr(1'b0));
  Register #(.width(32), .trigger("falling")) register_29 (.D(Din), .en(WE19), .Q(r19), .clk(Clock), .clr(1'b0));
  Register #(.width(32), .trigger("falling")) register_30 (.D(Din), .en(WE23), .Q(r23), .clk(Clock), .clr(1'b0));
  Register #(.width(32), .trigger("falling")) register_31 (.D(Din), .en(WE27), .Q(r27), .clk(Clock), .clr(1'b0));
  Register #(.width(32), .trigger("falling")) register_32 (.D(Din), .en(WE31), .Q(ra_Value), .clk(Clock), .clr(1'b0));
  Multiplexer #(.select(5), .width(32)) multiplexer_1 (
    .in0(r0), .in1(r1), .in2(v0_Value), .in3(r3), .in4(a0_Value), .in5(r5), .in6(r6), .in7(r7), .in8(r8),
    .in9(r9), .in10(r10), .in11(r11), .in12(r12), .in13(r13), .in14(r14), .in15(r15), .in16(s0_Value),
    .in17(s1_Value), .in18(s2_Value), .in19(r19), .in20(r20), .in21(r21), .in22(r22), .in23(r23), .in24(r24),
    .in25(r25), .in26(r26), .in27(r27), .in28(r28), .in29(r29), .in30(r30), .in31(ra_Value), .out(Reg1),
    .sel(Reg1_num), .en(1'b1));
  Multiplexer #(.select(5), .width(32)) multiplexer_2 (
    .in0(r0), .in1(r1), .in2(v0_Value), .in3(r3), .in4(a0_Value), .in5(r5), .in6(r6), .in7(r7), .in8(r8),
    .in9(r9), .in10(r10), .in11(r11), .in12(r12), .in13(r13), .in14(r14), .in15(r15), .in16(s0_Value),
    .in17(s1_Value), .in18(s2_Value), .in19(r19), .in20(r20), .in21(r21), .in22(r22), .in23(r23), .in24(r24),
    .in25(r25), .in26(r26), .in27(r27), .in28(r28), .in29(r29), .in30(r30), .in31(ra_Value), .out(Reg2_2),
    .sel(Reg2), .en(1'b1));

  // Other names for the same wires on the sheet: clk = Clock; r2[31:0] = v0_Value; r4[31:0] = a0_Value;
  //   ra[31:0] = ra_Value; reg2_num[4:0] = Reg2; reg2_t[31:0] = Reg2_2; s0[31:0] = s0_Value; s1[31:0] = s1_Value;
  //   s2[31:0] = s2_Value; WE = Write_Enable; write_data[31:0] = Din

  // Notes on the sheet:
  //   输入引脚
  //   输出引脚
  //   Debug引脚，便于观测寄存器值
  //   请勿修改引脚以及封装，直接使用隧道连接电路
endmodule

module test (
);

  wire undriven;

  main main_1 (.Clock(undriven));  // open: Reg1_num, Reg2, Write_Reg_num, Din, Write_Enable, Reg1, Reg2_2, s0_Value, s1_Value, s2_Value, ra_Value, v0_Value, a0_Value
endmodule
