// Logisim project mips单周期加中断.circ as structural Verilog: 7 circuits, main circuit main
module main (
);

  wire ALUSrc, and_4_out, and_5_out, and_6_out, beq, bgez, bne, button_1_out, button_2_out, button_3_out,
       clk, clock_1_out, comparator_1_eq, comparator_2_eq, comparator_3_eq, demultiplexer_1_out0,
       demultiplexer_1_out1, demultiplexer_1_out2, demultiplexer_1_out3, equal, eret, halt,
       interruptctrl_1_interrupt_flag, interruptctrl_1_out_6, interruptctrl_1_out_7, interruptctrl_1_out_8,
       j, jal, jr, MemRead, MemtoReg, MemWrite, mfc0, mtc0, not_1_out, not_2_out, or_1_out, or_2_out,
       or_3_out, or_4_out, or_5_out, or_6_out, or_7_out, RegDst, RegWrite, sb, Shamt_Sign, Sign, srav,
       systemcall;
  wire [3:0] ALUop;
  wire [4:0] bit_extender_4_out, multiplexer_4_out, multiplexer_5_out, multiplexer_6_out, multiplexer_8_out,
       multiplier_1_out, rd, rs, rt, shamt;
  wire [5:0] funct, OP;
  wire [7:0] ram_1_data, ram_2_data, ram_3_data, ram_4_data;
  wire [15:0] imme;
  wire [25:0] addr;
  wire [31:0] a0, adder_2_out, alu_1_result, and_3_out, bit_extender_1_out, bit_extender_2_out,
       bit_extender_3_out, I_imm, interruptctrl_1_interrupt_addr, main_1_s0_value, main_1_s1_value,
       main_1_s2_value, multiplexer_1_out, multiplexer_2_out, multiplexer_3_out, multiplexer_7_out,
       multiplexer_9_out, multiplexer_10_out, multiplexer_12_out, multiplexer_13_out, multiplexer_14_out,
       multiplexer_15_out, multiplexer_16_out, multiplexer_17_out, multiplexer_18_out, multiplexer_19_out,
       multiplexer_20_out, multiplexer_21_out, pc4, PC_2_q, PC_q, pcReturn, ra, register_1_q, rom_1_data,
       shifter_1_out, shifter_2_out, v0;

  Multiplexer #(.width(32), .enable("false")) multiplexer_1 (
    .in0(multiplexer_19_out), .in1(a0), .out(multiplexer_1_out), .sel(mtc0));
  or or_1 (or_1_out, interruptctrl_1_interrupt_flag, mtc0);
  Button button_1 (.out(button_1_out));
  Button button_2 (.out(button_2_out));
  Button button_3 (.out(button_3_out));
  Register #(.width(32)) EPC (.D(multiplexer_1_out), .en(or_1_out), .Q(pcReturn), .clk(clk));  // open: clr
  interruptCtrl interruptctrl_1 (
    .clk(clk), ._1(button_1_out), .out_6(interruptctrl_1_out_6), ._2(button_2_out),
    .out_7(interruptctrl_1_out_7), .eret(eret), ._3(button_3_out), .out_8(interruptctrl_1_out_8),
    .interrupt_flag(interruptctrl_1_interrupt_flag), .interrupt_addr(interruptctrl_1_interrupt_addr));
  not not_1 (not_1_out, systemcall);
  Control_Unit control_unit_1 (
    .op(OP), .funct(funct), .RegDst(RegDst), .ALUop(ALUop), .RegWrite(RegWrite), .Sign(Sign),
    .Shamt_Sign(Shamt_Sign), .MemRead(MemRead), .MemWrite(MemWrite), .MemtoReg(MemtoReg), .ALUSrc(ALUSrc),
    .beq(beq), .bne(bne), .j(j), .jal(jal), .jr(jr), .srav(srav), .bgez(bgez), .sb(sb), .mfc0(mfc0),
    .mtc0(mtc0));
  Multiplexer #(.width(32), .enable("false")) multiplexer_2 (
    .in0(multiplexer_19_out), .in1(pcReturn), .out(multiplexer_2_out), .sel(eret));
  Multiplexer #(.width(32), .enable("false")) multiplexer_3 (
    .in0(multiplexer_2_out), .in1(interruptctrl_1_interrupt_addr), .out(multiplexer_3_out),
    .sel(interruptctrl_1_interrupt_flag));
  LED led_1 (.in(interruptctrl_1_out_6));
  LED led_2 (.in(interruptctrl_1_out_7));
  LED led_3 (.in(interruptctrl_1_out_8));
  Clock clock_1 (.out(clock_1_out));
  Register #(.width(32)) register_1 (.D(a0), .Q(register_1_q), .clk(not_1_out));  // open: en, clr
  // Probe on multiplexer_19_out
  Adder #(.width(32)) adder_1 (.a(PC_q), .b(32'h4), .out(pc4));  // open: cin, cout
  Register #(.width(32)) PC (.D(multiplexer_3_out), .Q(PC_q), .clk(clk));  // open: en, clr
  // Probe on main_1_s0_value
  Multiplexer #(.width(5), .enable("false")) multiplexer_4 (
    .in0(rs), .in1(5'b00010), .out(multiplexer_4_out), .sel(systemcall));
  Multiplexer #(.width(5), .enable("false")) multiplexer_5 (
    .in0(rt), .in1(5'b00100), .out(multiplexer_5_out), .sel(systemcall));
  // Probe on PC_2_q
  Counter #(.width(32), .max('hffffffff)) PC_2 (.Q(PC_2_q), .clk(clk));  // open: load, D, count, carry, clr
  and and_1 (clk, clock_1_out, ~halt);  // AND_Gate
  Hex_Digit_Display hex_digit_display_1 (.value(register_1_q[27:24]));  // open: dp
  Hex_Digit_Display hex_digit_display_2 (.value(register_1_q[31:28]));  // open: dp
  // Probe on main_1_s2_value
  // Probe on main_1_s1_value
  Multiplexer #(.width(5), .enable("false")) multiplexer_6 (.in0(rt), .in1(rd), .out(multiplexer_6_out), .sel(RegDst));
  Hex_Digit_Display hex_digit_display_3 (.value(register_1_q[19:16]));  // open: dp
  Hex_Digit_Display hex_digit_display_4 (.value(register_1_q[23:20]));  // open: dp
  assign bit_extender_1_out = {{16{1'b0}}, imme};  // Bit_Extender bit_extender_1
  assign bit_extender_2_out = {{16{imme[15]}}, imme};  // Bit_Extender bit_extender_2
  Multiplexer #(.width(32), .enable("false")) multiplexer_7 (
    .in0({32{1'b0}}), .in1(v0), .out(multiplexer_7_out), .sel(systemcall));
  ROM #(.addrWidth(10), .dataWidth(32)) rom_1 (.addr(PC_q[11:2]), .data(rom_1_data));  // open: sel
  Multiplexer #(.width(5), .enable("false")) multiplexer_8 (
    .in0(multiplexer_6_out), .in1({5{1'b1}}), .out(multiplexer_8_out), .sel(jal));
  Multiplexer #(.width(32), .enable("false")) multiplexer_9 (
    .in0(multiplexer_10_out), .in1(pcReturn), .out(multiplexer_9_out), .sel(mfc0));
  Multiplexer #(.width(32), .enable("false")) multiplexer_10 (
    .in0(multiplexer_21_out), .in1(pc4), .out(multiplexer_10_out), .sel(jal));
  Hex_Digit_Display hex_digit_display_5 (.value(register_1_q[11:8]));  // open: dp
  Hex_Digit_Display hex_digit_display_6 (.value(register_1_q[15:12]));  // open: dp
  Multiplexer #(.width(32), .enable("false")) multiplexer_11 (
    .in0(bit_extender_1_out), .in1(bit_extender_2_out), .out(I_imm), .sel(Sign));
  Register #(.width(1)) register_2 (.D(comparator_1_eq), .Q(halt), .clk(clk));  // open: en, clr
  Comparator #(.width(32)) comparator_1 (.a(multiplexer_7_out), .b(32'ha), .eq(comparator_1_eq));  // open: gt, lt
  Decoder decoder_1 (
    .instruction(rom_1_data), .func(funct), .shamt(shamt), .rd(rd), .rt(rt), .rs(rs), .op(OP), .I_imed(imme),
    .J_imed(addr), .mfc0(mfc0), .mtc0(mtc0), .eret(eret));
  \CS1404_U201414667_甘鹏_regfile_main  main_1 (
    .Reg1_num(multiplexer_4_out), .Reg2(multiplexer_5_out), .Write_Reg_num(multiplexer_8_out),
    .Din(multiplexer_9_out), .Write_Enable(RegWrite), .Clock(clk), .Reg1(v0), .Reg2_2(a0),
    .s0_Value(main_1_s0_value), .s1_Value(main_1_s1_value), .s2_Value(main_1_s2_value), .ra_Value(ra));
  Hex_Digit_Display hex_digit_display_7 (.value(register_1_q[7:4]));  // open: dp
  Hex_Digit_Display hex_digit_display_8 (.value(register_1_q[3:0]));  // open: dp
  Multiplexer #(.width(32), .enable("false")) multiplexer_12 (
    .in0(a0), .in1(I_imm), .out(multiplexer_12_out), .sel(ALUSrc));
  assign bit_extender_3_out = {{27{1'b0}}, shamt};  // Bit_Extender bit_extender_3
  Multiplexer #(.width(32), .enable("false")) multiplexer_13 (
    .in0(v0), .in1(a0), .out(multiplexer_13_out), .sel(Shamt_Sign));
  Multiplexer #(.width(32), .enable("false")) multiplexer_14 (
    .in0(multiplexer_12_out), .in1(bit_extender_3_out), .out(multiplexer_14_out), .sel(Shamt_Sign));
  Comparator #(.width(6)) comparator_2 (.a(OP), .b({6{1'b0}}), .eq(comparator_2_eq));  // open: gt, lt
  and and_2 (systemcall, comparator_2_eq, comparator_3_eq);
  Comparator #(.width(6)) comparator_3 (.a(funct), .b(6'b001100), .eq(comparator_3_eq));  // open: gt, lt
  assign and_3_out = v0 & 32'h1f;  // AND_Gate and_3, 32 bits wide
  Shifter #(.width(32)) shifter_1 (.in(I_imm), .\dist (5'b00010), .out(shifter_1_out));
  and and_4 (and_4_out, beq, equal);
  and and_5 (and_5_out, ~equal, bne);  // AND_Gate
  Multiplexer #(.width(32), .enable("false")) multiplexer_15 (
    .in0(multiplexer_14_out), .in1(and_3_out), .out(multiplexer_15_out), .sel(srav));
  Adder #(.width(32)) adder_2 (.a(pc4), .b(shifter_1_out), .out(adder_2_out));  // open: cin, cout
  Multiplexer #(.width(32), .enable("false")) multiplexer_16 (
    .in0(multiplexer_15_out), .in1({32{1'b0}}), .out(multiplexer_16_out), .sel(bgez));
  Multiplexer #(.width(32), .enable("false")) multiplexer_17 (
    .in0(pc4), .in1(adder_2_out), .out(multiplexer_17_out), .sel(or_3_out));
  Multiplexer #(.width(32), .enable("false")) multiplexer_18 (
    .in0(multiplexer_17_out), .in1({pc4[31:28], addr, 2'b00}), .out(multiplexer_18_out), .sel(or_2_out));
  or or_2 (or_2_out, j, jal);
  or or_3 (or_3_out, and_4_out, and_6_out, and_5_out);
  and and_6 (and_6_out, bgez, not_2_out);
  not not_2 (not_2_out, alu_1_result[0]);
  ALU alu_1 (
    .AluOP(ALUop), .X(multiplexer_13_out), .Equal(equal), .Result(alu_1_result), .Y(multiplexer_16_out));  // open: Signed_Overflow, Result_2, UnSigned_Overflow
  Multiplexer #(.width(32), .enable("false")) multiplexer_19 (
    .in0(multiplexer_18_out), .in1(v0), .out(multiplexer_19_out), .sel(jr));
  assign bit_extender_4_out = {{3{1'b0}}, alu_1_result[1:0]};  // Bit_Extender bit_extender_4
  Multiplier #(.width(5)) multiplier_1 (
    .a(bit_extender_4_out), .b(5'b01000), .out(multiplier_1_out));  // open: cin, cout
  Demultiplexer #(.select(2), .enable("false")) demultiplexer_1 (
    .out0(demultiplexer_1_out0), .out1(demultiplexer_1_out1), .out2(demultiplexer_1_out2),
    .out3(demultiplexer_1_out3), .in(1'b1), .sel(alu_1_result[1:0]));
  // Probe on addr
  // Probe on OP
  // Probe on rs
  // Probe on rt
  // Probe on rd
  // Probe on shamt
  // Probe on imme
  // Probe on funct
  Multiplexer #(.width(32), .enable("false")) multiplexer_20 (
    .in0(a0), .in1(shifter_2_out), .out(multiplexer_20_out), .sel(sb));
  Shifter #(.width(32)) shifter_2 (.in(a0), .\dist (multiplier_1_out), .out(shifter_2_out));
  or or_4 (or_4_out, ~sb, demultiplexer_1_out0);  // OR_Gate
  or or_5 (or_5_out, ~sb, demultiplexer_1_out1);  // OR_Gate
  or or_6 (or_6_out, ~sb, demultiplexer_1_out2);  // OR_Gate
  or or_7 (or_7_out, ~sb, demultiplexer_1_out3);  // OR_Gate
  RAM #(.addrWidth(10), .bus("separate")) ram_1 (
    .addr(alu_1_result[11:2]), .din(multiplexer_20_out[7:0]), .data(ram_1_data), .str(MemWrite),
    .sel(or_4_out), .clk(clk), .ld(MemRead));  // open: clr
  RAM #(.addrWidth(10), .bus("separate")) ram_2 (
    .addr(alu_1_result[11:2]), .din(multiplexer_20_out[15:8]), .data(ram_2_data), .str(MemWrite),
    .sel(or_5_out), .clk(clk), .ld(MemRead));  // open: clr
  RAM #(.addrWidth(10), .bus("separate")) ram_3 (
    .addr(alu_1_result[11:2]), .din(multiplexer_20_out[23:16]), .data(ram_3_data), .str(MemWrite),
    .sel(or_6_out), .clk(clk), .ld(MemRead));  // open: clr
  RAM #(.addrWidth(10), .bus("separate")) ram_4 (
    .addr(alu_1_result[11:2]), .din(multiplexer_20_out[31:24]), .data(ram_4_data), .str(MemWrite),
    .sel(or_7_out), .clk(clk), .ld(MemRead));  // open: clr
  Multiplexer #(.width(32), .enable("false")) multiplexer_21 (
    .in0(alu_1_result), .in1({ram_4_data, ram_3_data, ram_2_data, ram_1_data}), .out(multiplexer_21_out),
    .sel(MemtoReg));

  // Other names for the same wires on the sheet: Din[31:0] = a0

  // Notes on the sheet:
  //   contents of rom_1 (hex, n*v repeats v):
  //   8000c99 8000c35 8000c67 23bdfffc afa80000 23bdfffc afa90000 23bdfffc afb00000 23bdfffc afb10000
  //   23bdfffc afb20000 23bdfffc afb30000 40108800 23bdfffc afb00000 20080008 20090001 20130003 132020
  //   20020022 c 139900 1094022 1500fffa 20080008 20090001 20130003 139f00 132020 20020022 c 139902
  //   1094022 1500fffa 8fb00000 27bd0004 40908800 8fb30000 27bd0004 8fb20000 27bd0004 8fb10000 27bd0004
  //   8fb00000 27bd0004 8fa90000 27bd0004 8fa80000 27bd0004 42000018 23bdfffc afa80000 23bdfffc afa90000
  //   23bdfffc afb00000 23bdfffc afb10000 23bdfffc afb20000 23bdfffc afb30000 40108800 23bdfffc afb00000
  //   20080008 20090001 20130001 132020 20020022 c 139900 1094022 1500fffa 20080008 20090001 20130001
  //   139f00 132020 20020022 c 139902 1094022 1500fffa 8fb00000 27bd0004 40908800 8fb30000 27bd0004
  //   8fb20000 27bd0004 8fb10000 27bd0004 8fb00000 27bd0004 8fa90000 27bd0004 8fa80000 27bd0004 42000018
  //   23bdfffc afa80000 23bdfffc afa90000 23bdfffc afb00000 23bdfffc afb10000 23bdfffc afb20000 23bdfffc
  //   afb30000 40108800 23bdfffc afb00000 20080008 20090001 20130002 132020 20020022 c 139900 1094022
  //   1500fffa 20080008 20090001 20130002 139f00 132020 20020022 c 139902 1094022 1500fffa 8fb00000
  //   27bd0004 40908800 8fb30000 27bd0004 8fb20000 27bd0004 8fb10000 27bd0004 8fb00000 27bd0004 8fa90000
  //   27bd0004 8fa80000 27bd0004 42000018 3c010000 3421ffff 3a1e821 20110001 8000ca1 20110001 20120002
  //   20130003 8000ca5 20110001 20120002 20130003 8000ca9 20110001 20120002 20130003 8000cad 20110001
  //   20120002 20130003 c000d54 20100001 20110001 118fc0 112020 20020022 c 118882 12200001 8000cb1 112020
  //   20020022 c 20110001 118880 112020 20020022 c 12200001 8000cbb 20110001 118fc0 112020 20020022 c
  //   1188c3 112020 20020022 c 118903 112020 20020022 c 118903 112020 20020022 c 118903 112020 20020022 c
  //   118903 112020 20020022 c 118903 112020 20020022 c 118903 112020 20020022 c 118903 112020 20020022 c
  //   20100001 109fc0 139fc3 8021 2012000c 24160003 26100001 3210000f 20080008 20090001 139900 2709825
  //   132020 20020022 c 1094022 1500fff9 22100001 2018000f 2188024 108700 20080008 20090001 139902 2709825
  //   132021 20020022 c 1094022 1500fff9 108702 2c9b022 12c00001 8000cec 4020 1084027 84400 3508ffff 82021
  //   20020022 c 2010ffff 20110000 ae300000 22100001 22310004 ae300000 22100001 22310004 ae300000 22100001
  //   22310004 ae300000 22100001 22310004 ae300000 22100001 22310004 ae300000 22100001 22310004 ae300000
  //   22100001 22310004 ae300000 22100001 22310004 ae300000 22100001 22310004 ae300000 22100001 22310004
  //   ae300000 22100001 22310004 ae300000 22100001 22310004 ae300000 22100001 22310004 ae300000 22100001
  //   22310004 ae300000 22100001 22310004 ae300000 22100001 22310004 22100001 8020 2011003c 8e130000
  //   8e340000 274402a 11000002 ae330000 ae140000 2231fffc 1611fff8 102020 20020022 c 22100004 2011003c
  //   1611fff2 2002000a c 20100000 22100001 102020 20020022 c 22100002 102020 20020022 c 22100003 102020
  //   20020022 c 22100004 102020 20020022 c 22100005 102020 20020022 c 22100006 102020 20020022 c 22100007
  //   102020 20020022 c 22100008 102020 20020022 20020022 c 3e00008
endmodule

module Control_Unit (
  input  [5:0] op,
  input  [5:0] funct,
  input  mfc0,
  input  mtc0,
  output RegDst,
  output [3:0] ALUop,
  output RegWrite,
  output Sign,
  output Shamt_Sign,
  output MemRead,
  output MemWrite,
  output MemtoReg,
  output ALUSrc,
  output beq,
  output bne,
  output j,
  output jal,
  output jr,
  output srav,
  output bgez,
  output sb
);

  wire add, addi, addiu, addu, \and , andi, \nor , \or , or_2_out, ori, sll, slt, slti, sltiu, sltu, sra,
       srl, sub, sw;

  I_type i_type_1 (
    .op5(op[5]), .op4(op[4]), .op3(op[3]), .op2(op[2]), .op1(op[1]), .op0(op[0]), .addi(addi), .addiu(addiu),
    .andi(andi), .ori(ori), .lw(MemtoReg), .sw(sw), .beq(beq), .bne(bne), .slti(slti), .j(j), .jal(jal),
    .fenable(RegDst), .sltiu(sltiu), .sb(sb), .bgez(bgez));
  R_type r_type_1 (
    .fenable(RegDst), .funct5(funct[5]), .funct4(funct[4]), .funct3(funct[3]), .funct2(funct[2]),
    .funct1(funct[1]), .funct0(funct[0]), .add(add), .addu(addu), .\and (\and ), .sll(sll), .sra(sra),
    .srl(srl), .sub(sub), .\or (\or ), .\nor (\nor ), .slt(slt), .sltu(sltu), .jr(jr), .srav(srav));
  or or_1 (RegWrite, sltiu, add, addu, \and , sll, sra, srl, sub, \or , \nor , sltu, addi, addiu, andi, ori, MemtoReg, slti, slt, jal, or_2_out);
  or or_2 (or_2_out, srav, mfc0);
  or or_3 (Sign, sb, addi, MemtoReg, sw, beq, bne, slti, bgez);
  or or_4 (Shamt_Sign, sll, sra, srav, srl);
  or or_5 (ALUSrc, sltiu, addi, addiu, andi, ori, MemtoReg, sw, slti, sb);
  or or_6 (ALUop[3], sltiu, \or , ori, \nor , slt, slti, sltu, bgez);
  or or_7 (ALUop[2], sltiu, add, addi, addu, addiu, \and , sub, andi, MemtoReg, sw, sltu, sb);
  or or_8 (ALUop[1], bgez, andi, sub, \nor , slt, slti, srl, \and );
  or or_9 (ALUop[0], bgez, srav, addi, addu, addiu, \and , andi, sra, slti, MemtoReg, sw, slt, add, sb);
  or or_10 (MemRead, MemtoReg, sb);
  or or_11 (MemWrite, sb, sw);

  // Other names for the same wires on the sheet: lw = MemtoReg
endmodule

module Decoder (
  input  [31:0] instruction,
  output mfc0,
  output [5:0] func,
  output [4:0] shamt,
  output [4:0] rd,
  output mtc0,
  output [4:0] rt,
  output [4:0] rs,
  output [5:0] op,
  output [15:0] I_imed,
  output [25:0] J_imed,
  output eret
);

  wire comparator_1_eq, comparator_2_eq, comparator_3_eq;

  Comparator #(.width(5)) comparator_1 (.a(instruction[25:21]), .b({5{1'b0}}), .eq(comparator_1_eq));  // open: gt, lt
  Comparator #(.width(5)) comparator_2 (.a(instruction[25:21]), .b(5'b00100), .eq(comparator_2_eq));  // open: gt, lt
  Comparator #(.width(6)) comparator_3 (.a(instruction[31:26]), .b(6'b010000), .eq(comparator_3_eq));  // open: gt, lt
  Comparator #(.width(32)) comparator_4 (.a(32'h42000018), .b(instruction), .eq(eret));  // open: gt, lt
  and and_1 (mfc0, comparator_1_eq, comparator_3_eq);
  and and_2 (mtc0, comparator_2_eq, comparator_3_eq);

  assign func = instruction[5:0];
  assign I_imed = instruction[15:0];
  assign J_imed = instruction[25:0];
  assign op = instruction[31:26];
  assign rd = instruction[15:11];
  assign rs = instruction[25:21];
  assign rt = instruction[20:16];
  assign shamt = instruction[10:6];
endmodule

module I_type (
  input  op5,
  input  op4,
  input  op3,
  input  op2,
  input  op1,
  input  op0,
  output addi,
  output addiu,
  output andi,
  output ori,
  output lw,
  output sw,
  output beq,
  output bne,
  output slti,
  output j,
  output jal,
  output sltiu,
  output sb,
  output bgez,
  output fenable
);

  wire not_1_out, not_2_out, not_3_out, not_4_out, not_5_out, not_6_out, not_7_out, not_8_out, not_9_out,
       not_10_out, not_11_out, not_12_out, not_13_out, not_14_out, not_15_out, not_16_out, not_17_out,
       not_18_out, not_19_out, not_20_out, not_21_out, not_22_out, not_23_out, not_24_out, not_25_out,
       not_26_out, not_27_out, not_28_out, not_29_out, not_30_out, not_31_out, not_32_out, not_33_out,
       not_34_out, not_35_out, not_36_out, not_37_out, not_38_out, not_39_out, not_40_out, not_41_out,
       not_42_out, not_43_out, not_44_out, not_45_out, not_46_out, not_47_out, not_48_out, not_49_out,
       not_50_out, not_51_out, not_52_out, not_53_out, not_54_out, not_55_out, not_56_out, not_57_out,
       not_58_out, not_59_out, not_60_out, not_61_out;

  not not_1 (not_1_out, op5);
  not not_2 (not_2_out, op4);
  not not_3 (not_3_out, op2);
  not not_4 (not_4_out, op1);
  not not_5 (not_5_out, op0);
  not not_6 (not_6_out, op5);
  not not_7 (not_7_out, op4);
  not not_8 (not_8_out, op2);
  not not_9 (not_9_out, op1);
  not not_10 (not_10_out, op5);
  not not_11 (not_11_out, op4);
  not not_12 (not_12_out, op1);
  not not_13 (not_13_out, op0);
  not not_14 (not_14_out, op5);
  not not_15 (not_15_out, op4);
  not not_16 (not_16_out, op1);
  not not_17 (not_17_out, op4);
  not not_18 (not_18_out, op3);
  not not_19 (not_19_out, op2);
  not not_20 (not_20_out, op4);
  not not_21 (not_21_out, op2);
  not not_22 (not_22_out, op5);
  not not_23 (not_23_out, op4);
  not not_24 (not_24_out, op3);
  not not_25 (not_25_out, op1);
  not not_26 (not_26_out, op0);
  not not_27 (not_27_out, op5);
  not not_28 (not_28_out, op4);
  not not_29 (not_29_out, op3);
  not not_30 (not_30_out, op1);
  not not_31 (not_31_out, op5);
  not not_32 (not_32_out, op4);
  not not_33 (not_33_out, op2);
  not not_34 (not_34_out, op0);
  not not_35 (not_35_out, op5);
  not not_36 (not_36_out, op4);
  not not_37 (not_37_out, op3);
  not not_38 (not_38_out, op2);
  not not_39 (not_39_out, op0);
  not not_40 (not_40_out, op5);
  not not_41 (not_41_out, op4);
  not not_42 (not_42_out, op3);
  not not_43 (not_43_out, op2);
  not not_44 (not_44_out, op5);
  not not_45 (not_45_out, op4);
  not not_46 (not_46_out, op2);
  not not_47 (not_47_out, op4);
  not not_48 (not_48_out, op2);
  not not_49 (not_49_out, op1);
  not not_50 (not_50_out, op0);
  not not_51 (not_51_out, op5);
  not not_52 (not_52_out, op4);
  not not_53 (not_53_out, op3);
  not not_54 (not_54_out, op2);
  not not_55 (not_55_out, op1);
  not not_56 (not_56_out, op5);
  not not_57 (not_57_out, op4);
  not not_58 (not_58_out, op3);
  not not_59 (not_59_out, op2);
  not not_60 (not_60_out, op1);
  not not_61 (not_61_out, op0);
  and and_1 (addi, not_1_out, not_2_out, op3, not_3_out, not_4_out, not_5_out);
  and and_2 (addiu, not_6_out, not_7_out, op3, not_8_out, not_9_out, op0);
  and and_3 (andi, not_10_out, not_11_out, op3, op2, not_12_out, not_13_out);
  and and_4 (ori, not_14_out, not_15_out, op3, op2, not_16_out, op0);
  and and_5 (lw, op5, not_17_out, not_18_out, not_19_out, op1, op0);
  and and_6 (sw, op5, not_20_out, op3, not_21_out, op1, op0);
  and and_7 (beq, not_22_out, not_23_out, not_24_out, op2, not_25_out, not_26_out);
  and and_8 (bne, not_27_out, not_28_out, not_29_out, op2, not_30_out, op0);
  and and_9 (slti, not_31_out, not_32_out, op3, not_33_out, op1, not_34_out);
  and and_10 (j, not_35_out, not_36_out, not_37_out, not_38_out, op1, not_39_out);
  and and_11 (jal, not_40_out, not_41_out, not_42_out, not_43_out, op1, op0);
  and and_12 (sltiu, not_44_out, not_45_out, op3, not_46_out, op1, op0);
  and and_13 (sb, op5, not_47_out, op3, not_48_out, not_49_out, not_50_out);
  and and_14 (bgez, not_51_out, not_52_out, not_53_out, not_54_out, not_55_out, op0);
  and and_15 (fenable, not_56_out, not_57_out, not_58_out, not_59_out, not_60_out, not_61_out);
endmodule

module R_type (
  input  fenable,
  input  funct5,
  input  funct4,
  input  funct3,
  input  funct2,
  input  funct1,
  input  funct0,
  output add,
  output addu,
  output \and ,
  output sll,
  output sra,
  output srl,
  output sub,
  output \or ,
  output \nor ,
  output slt,
  output sltu,
  output jr,
  output srav
);

  wire and_1_out, and_2_out, and_3_out, and_4_out, and_5_out, and_6_out, and_7_out, and_8_out, and_9_out,
       and_10_out, and_11_out, and_12_out, and_13_out, not_1_out, not_2_out, not_3_out, not_4_out, not_5_out,
       not_6_out, not_7_out, not_8_out, not_9_out, not_10_out, not_11_out, not_12_out, not_13_out,
       not_14_out, not_15_out, not_16_out, not_17_out, not_18_out, not_19_out, not_20_out, not_21_out,
       not_22_out, not_23_out, not_24_out, not_25_out, not_26_out, not_27_out, not_28_out, not_29_out,
       not_30_out, not_31_out, not_32_out, not_33_out, not_34_out, not_35_out, not_36_out, not_37_out,
       not_38_out, not_39_out, not_40_out, not_41_out, not_42_out, not_43_out, not_44_out, not_45_out,
       not_46_out, not_47_out, not_48_out, not_49_out, not_50_out;

  not not_1 (not_1_out, funct4);
  not not_2 (not_2_out, funct3);
  not not_3 (not_3_out, funct2);
  not not_4 (not_4_out, funct1);
  not not_5 (not_5_out, funct0);
  not not_6 (not_6_out, funct4);
  not not_7 (not_7_out, funct3);
  not not_8 (not_8_out, funct2);
  not not_9 (not_9_out, funct1);
  not not_10 (not_10_out, funct4);
  not not_11 (not_11_out, funct3);
  not not_12 (not_12_out, funct1);
  not not_13 (not_13_out, funct0);
  not not_14 (not_14_out, funct5);
  not not_15 (not_15_out, funct4);
  not not_16 (not_16_out, funct3);
  not not_17 (not_17_out, funct2);
  not not_18 (not_18_out, funct1);
  not not_19 (not_19_out, funct0);
  not not_20 (not_20_out, funct5);
  not not_21 (not_21_out, funct4);
  not not_22 (not_22_out, funct3);
  not not_23 (not_23_out, funct2);
  not not_24 (not_24_out, funct5);
  not not_25 (not_25_out, funct4);
  not not_26 (not_26_out, funct3);
  not not_27 (not_27_out, funct2);
  not not_28 (not_28_out, funct0);
  not not_29 (not_29_out, funct4);
  not not_30 (not_30_out, funct3);
  not not_31 (not_31_out, funct2);
  not not_32 (not_32_out, funct0);
  not not_33 (not_33_out, funct4);
  not not_34 (not_34_out, funct3);
  not not_35 (not_35_out, funct1);
  not not_36 (not_36_out, funct4);
  not not_37 (not_37_out, funct3);
  not not_38 (not_38_out, funct4);
  not not_39 (not_39_out, funct2);
  not not_40 (not_40_out, funct0);
  not not_41 (not_41_out, funct4);
  not not_42 (not_42_out, funct2);
  not not_43 (not_43_out, funct5);
  not not_44 (not_44_out, funct4);
  not not_45 (not_45_out, funct2);
  not not_46 (not_46_out, funct1);
  not not_47 (not_47_out, funct0);
  not not_48 (not_48_out, funct5);
  not not_49 (not_49_out, funct4);
  not not_50 (not_50_out, funct3);
  and and_1 (and_1_out, funct5, not_1_out, not_2_out, not_3_out, not_4_out, not_5_out);
  and and_2 (and_2_out, funct5, not_6_out, not_7_out, not_8_out, not_9_out, funct0);
  and and_3 (and_3_out, funct5, not_10_out, not_11_out, funct2, not_12_out, not_13_out);
  and and_4 (and_4_out, not_14_out, not_15_out, not_16_out, not_17_out, not_18_out, not_19_out);
  and and_5 (and_5_out, not_20_out, not_21_out, not_22_out, not_23_out, funct1, funct0);
  and and_6 (and_6_out, not_24_out, not_25_out, not_26_out, not_27_out, funct1, not_28_out);
  and and_7 (and_7_out, funct5, not_29_out, not_30_out, not_31_out, funct1, not_32_out);
  and and_8 (and_8_out, funct5, not_33_out, not_34_out, funct2, not_35_out, funct0);
  and and_9 (and_9_out, funct5, not_36_out, not_37_out, funct2, funct1, funct0);
  and and_10 (and_10_out, funct5, not_38_out, funct3, not_39_out, funct1, not_40_out);
  and and_11 (and_11_out, funct5, not_41_out, funct3, not_42_out, funct1, funct0);
  and and_12 (and_12_out, not_43_out, not_44_out, funct3, not_45_out, not_46_out, not_47_out);
  and and_13 (and_13_out, not_48_out, not_49_out, not_50_out, funct2, funct1, funct0);
  and and_14 (add, fenable, and_1_out);
  and and_15 (addu, fenable, and_2_out);
  and and_16 (\and , fenable, and_3_out);
  and and_17 (sll, fenable, and_4_out);
  and and_18 (sra, fenable, and_5_out);
  and and_19 (srl, fenable, and_6_out);
  and and_20 (sub, fenable, and_7_out);
  and and_21 (\or , fenable, and_8_out);
  and and_22 (\nor , fenable, and_9_out);
  and and_23 (slt, fenable, and_10_out);
  and and_24 (sltu, fenable, and_11_out);
  and and_25 (jr, fenable, and_12_out);
  and and_26 (srav, fenable, and_13_out);
endmodule

module interruptCtrl (
  input  clk,
  input  _1,
  input  _2,
  input  eret,
  input  _3,
  output out_6,
  output out_7,
  output out_8,
  output interrupt_flag,
  output [31:0] interrupt_addr
);

  wire and_1_out, and_2_out, d_ff_1_q, d_ff_2_q, d_ff_3_q, d_ff_4_q, d_ff_5_q, d_ff_6_q, d_ff_8_q, d_ff_8_qn,
       d_ff_9_q, d_ff_9_qn, demultiplexer_1_out0, demultiplexer_1_out1, demultiplexer_1_out2,
       demultiplexer_1_out3, or_4_out;
  wire [1:0] d_ff_10_q, priority_encoder_1_out;

  D_Flip_Flop d_ff_1 (.clk(_1), .D(1'b1), .Q(d_ff_1_q), .reset(d_ff_4_q));  // open: Qn, preset, en
  D_Flip_Flop d_ff_2 (.clk(_2), .D(1'b1), .Q(d_ff_2_q), .reset(d_ff_5_q));  // open: Qn, preset, en
  D_Flip_Flop d_ff_3 (.clk(_3), .D(1'b1), .Q(d_ff_3_q), .reset(d_ff_6_q));  // open: Qn, preset, en
  D_Flip_Flop d_ff_4 (.clk(clk), .D(d_ff_1_q), .Q(d_ff_4_q), .en(and_1_out));  // open: Qn, preset, reset
  D_Flip_Flop d_ff_5 (.clk(clk), .D(d_ff_2_q), .Q(d_ff_5_q), .en(d_ff_9_qn));  // open: Qn, preset, reset
  D_Flip_Flop d_ff_6 (.clk(clk), .D(d_ff_3_q), .Q(d_ff_6_q));  // open: Qn, preset, en, reset
  D_Flip_Flop d_ff_7 (.preset(d_ff_4_q), .reset(demultiplexer_1_out0));  // open: clk, D, Q, Qn, en
  D_Flip_Flop d_ff_8 (
    .Q(d_ff_8_q), .Qn(d_ff_8_qn), .preset(d_ff_5_q), .reset(demultiplexer_1_out1));  // open: clk, D, en
  D_Flip_Flop d_ff_9 (.Q(d_ff_9_q), .Qn(d_ff_9_qn), .preset(d_ff_6_q), .reset(or_4_out));  // open: clk, D, en
  or or_1 (out_6, d_ff_1_q, d_ff_4_q);
  and and_1 (and_1_out, ~out_7, and_2_out);  // AND_Gate
  or or_2 (out_7, d_ff_2_q, d_ff_5_q);
  or or_3 (out_8, d_ff_3_q, d_ff_6_q);
  Priority_Encoder #(.select(2)) priority_encoder_1 (
    .in1(d_ff_4_q), .in2(d_ff_5_q), .in3(d_ff_6_q), .out(priority_encoder_1_out), .gs(interrupt_flag),
    .en_in(1'b1));  // open: in0, en_out
  and and_2 (and_2_out, d_ff_8_qn, d_ff_9_qn);
  Multiplexer #(.select(2), .width(32)) multiplexer_1 (
    .in1(32'h4), .in2(32'h8), .in3(32'hc), .out(interrupt_addr), .sel(priority_encoder_1_out),
    .en(interrupt_flag));  // open: in0
  D_Flip_Flop d_ff_10 (.clk(clk), .D(d_ff_8_q), .Q(d_ff_10_q[0]));  // open: Qn, preset, en, reset
  D_Flip_Flop d_ff_11 (.clk(clk), .D(d_ff_9_q), .Q(d_ff_10_q[1]));  // open: Qn, preset, en, reset
  or or_4 (or_4_out, demultiplexer_1_out2, demultiplexer_1_out3);
  Demultiplexer #(.select(2), .enable("false")) demultiplexer_1 (
    .out0(demultiplexer_1_out0), .out1(demultiplexer_1_out1), .out2(demultiplexer_1_out2),
    .out3(demultiplexer_1_out3), .in(eret), .sel(d_ff_10_q));
endmodule

module temp (
  input  clk,
  input  _1,
  input  _2,
  input  reset,
  input  _3,
  input  reset_2,
  input  _11,
  input  _22,
  input  _33,
  output out_10,
  output out_11,
  output out_12,
  output interrupt_flag,
  output [31:0] interrupt_addr
);

  wire and_1_out, and_2_out, and_3_out, and_4_out, and_5_out, d_ff_1_q, d_ff_2_q, d_ff_3_q, d_ff_4_q,
       d_ff_5_q, d_ff_6_q, not_1_out, or_1_out, or_2_out;
  wire [1:0] priority_encoder_1_out;

  D_Flip_Flop d_ff_1 (.clk(_1), .D(1'b1), .Q(d_ff_1_q), .reset(d_ff_4_q));  // open: Qn, preset, en
  D_Flip_Flop d_ff_2 (.clk(_2), .D(1'b1), .Q(d_ff_2_q), .reset(d_ff_5_q));  // open: Qn, preset, en
  D_Flip_Flop d_ff_3 (.clk(_3), .D(1'b1), .Q(d_ff_3_q), .reset(d_ff_6_q));  // open: Qn, preset, en
  or or_1 (or_1_out, d_ff_2_q, d_ff_5_q);
  and and_1 (and_1_out, or_1_out, ~reset);  // AND_Gate
  or or_2 (or_2_out, d_ff_3_q, d_ff_6_q);
  and and_2 (and_2_out, or_2_out, ~reset_2);  // AND_Gate
  D_Flip_Flop d_ff_4 (.clk(clk), .D(d_ff_1_q), .Q(d_ff_4_q));  // open: Qn, preset, en, reset
  D_Flip_Flop d_ff_5 (.clk(clk), .D(and_1_out), .Q(d_ff_5_q));  // open: Qn, preset, en, reset
  D_Flip_Flop d_ff_6 (.clk(clk), .D(and_2_out), .Q(d_ff_6_q));  // open: Qn, preset, en, reset
  and and_3 (and_3_out, d_ff_4_q, ~_11);  // AND_Gate
  and and_4 (and_4_out, d_ff_5_q, ~_22);  // AND_Gate
  and and_5 (and_5_out, d_ff_6_q, ~_33);  // AND_Gate
  not not_1 (not_1_out, 1'b1);
  or or_3 (out_10, d_ff_1_q, d_ff_4_q);
  or or_4 (out_11, d_ff_2_q, d_ff_5_q);
  or or_5 (out_12, d_ff_3_q, d_ff_6_q);
  Priority_Encoder #(.select(2)) priority_encoder_1 (
    .in0(and_3_out), .in1(and_4_out), .in2(and_5_out), .in3(not_1_out), .out(priority_encoder_1_out),
    .gs(interrupt_flag), .en_in(1'b1));  // open: en_out
  Multiplexer #(.select(2), .width(32)) multiplexer_1 (
    .in0(32'h4), .in1(32'h8), .in2(32'hc), .out(interrupt_addr), .sel(priority_encoder_1_out),
    .en(interrupt_flag));  // open: in3
endmodule
