// Logisim project mips理想流水线.circ as structural Verilog: 12 circuits, main circuit pipeline
module pipeline (
);

  wire alu_1_equal, ALUSrc, beq, bgez, bne, clk, clock_1_out, comparator_1_eq, demultiplexer_1_out0,
       demultiplexer_1_out1, demultiplexer_1_out2, demultiplexer_1_out3, equal, halt, id_ex_1_beq_2,
       id_ex_1_bgez_2, id_ex_1_bne_2, id_ex_1_halt_2, id_ex_1_j_2, id_ex_1_jal_2, id_ex_1_jr_2,
       id_ex_1_memread_2, id_ex_1_memtoreg_2, id_ex_1_memwrite_2, id_ex_1_regdst_2, id_ex_1_regwrite_2,
       id_ex_1_sb_2, if_id_1_beq, if_id_1_bne, if_id_1_j, if_id_1_jal, if_id_1_jr, if_id_1_memread,
       if_id_1_memtoreg, if_id_1_memwrite, if_id_1_regdst, if_id_1_regwrite, if_id_1_sb, if_id_1_systemcall,
       j, jal, jr, mem_wb_1_halt_2, mem_wb_1_regwrite_2, MemRead, MemtoReg, MemWrite, not_1_out, or_1_out,
       or_2_out, or_3_out, or_4_out, RegDst, register_1_q, RegWrite, reset, sb, Shamt_Sign, srav;
  wire [3:0] ALUop, if_id_1_aluop;
  wire [4:0] bit_extender_1_out, if_id_1_out_24, if_id_1_out_26, mem_wb_1_rw, multiplexer_3_out,
       multiplexer_4_out, multiplier_1_out, shamt;
  wire [7:0] ram_1_data, ram_2_data, ram_3_data, ram_4_data;
  wire [25:0] ex_mem_1_addr_2, id_ex_1_out_35, if_id_1_out_20;
  wire [31:0] adder_1_out, alu_1_result, branch_1_branch_pc, Din, ex_mem_1_i_imm_2, ex_mem_1_result_2, I_imm,
       IC_q, id_ex_1_din_2, id_ex_1_out_33, id_ex_1_out_39, id_ex_1_out_42, id_ex_1_pc_2, id_ex_1_v0_2,
       if_id_1_ir_2, if_id_1_pc_2, IR, IRtoBP, main_1_reg1, main_1_reg2_2, main_1_s0_value, main_1_s1_value,
       main_1_s2_value, mem_wb_1_din_2, mem_wb_1_ir_2, mem_wb_1_pc_2, multiplexer_1_out, multiplexer_2_out,
       multiplexer_5_out, multiplexer_6_out, PC, PC_q, register_2_q, rom_1_data, shifter_1_out, toalu_1_x,
       toalu_1_y, v0;

  Register #(.width(32)) u_PC (.D(multiplexer_1_out), .Q(PC_q), .clk(clk));  // open: en, clr
  Multiplexer #(.width(32), .enable("false")) multiplexer_1 (
    .in0(adder_1_out), .in1(branch_1_branch_pc), .out(multiplexer_1_out), .sel(reset));
  Adder #(.width(32)) adder_1 (.a(PC_q), .b(32'h4), .out(adder_1_out));  // open: cin, cout
  ROM #(.addrWidth(10), .dataWidth(32)) rom_1 (.addr(PC_q[11:2]), .data(rom_1_data));  // open: sel
  IF_ID if_id_1 (
    .PC(PC_q), .IR(rom_1_data), .PC_2(if_id_1_pc_2), .IR_2(if_id_1_ir_2), .systemcall(if_id_1_systemcall),
    .RegDst(if_id_1_regdst), .ALUop(if_id_1_aluop), .RegWrite(if_id_1_regwrite), .Shamt_Sign(Shamt_Sign),
    .MemRead(if_id_1_memread), .MemWrite(if_id_1_memwrite), .MemtoReg(if_id_1_memtoreg), .ALUSrc(ALUSrc),
    .beq(if_id_1_beq), .bne(if_id_1_bne), .j(if_id_1_j), .jal(if_id_1_jal), .jr(if_id_1_jr), .srav(srav),
    .bgez(bgez), .sb(if_id_1_sb), .out_15(shamt), .out_17(I_imm), .out_20(if_id_1_out_20),
    .out_24(if_id_1_out_24), .out_26(if_id_1_out_26), .clk(clk), .reset(reset));  // open: out_27
  Multiplexer #(.width(32), .enable("false")) multiplexer_2 (
    .in0({32{1'b0}}), .in1(main_1_reg1), .out(multiplexer_2_out), .sel(if_id_1_systemcall));
  Multiplexer #(.width(5), .enable("false")) multiplexer_3 (
    .in0(if_id_1_out_24), .in1(5'b00010), .out(multiplexer_3_out), .sel(if_id_1_systemcall));
  Multiplexer #(.width(5), .enable("false")) multiplexer_4 (
    .in0(if_id_1_out_26), .in1(5'b00100), .out(multiplexer_4_out), .sel(if_id_1_systemcall));
  Comparator #(.width(32)) comparator_1 (.a(multiplexer_2_out), .b(32'ha), .eq(comparator_1_eq));  // open: gt, lt
  // Probe on main_1_s0_value
  Register #(.width(1)) register_1 (.D(comparator_1_eq), .Q(register_1_q), .clk(clk));  // open: en, clr
  // Probe on if_id_1_pc_2
  // Probe on if_id_1_ir_2
  // Probe on main_1_s1_value
  not not_1 (not_1_out, if_id_1_systemcall);
  // Probe on main_1_s2_value
  \CS1404_U201414667_甘鹏_regfile_main  main_1 (
    .Reg1_num(multiplexer_3_out), .Reg2(multiplexer_4_out), .Write_Reg_num(mem_wb_1_rw),
    .Din(mem_wb_1_din_2), .Write_Enable(mem_wb_1_regwrite_2), .Clock(clk), .Reg1(main_1_reg1),
    .Reg2_2(main_1_reg2_2), .s0_Value(main_1_s0_value), .s1_Value(main_1_s1_value), .s2_Value(main_1_s2_value));  // open: ra_Value
  Hex_Digit_Display hex_digit_display_1 (.value(register_2_q[31:28]));  // open: dp
  Register #(.width(32)) register_2 (.D(main_1_reg2_2), .Q(register_2_q), .clk(not_1_out));  // open: en, clr
  Hex_Digit_Display hex_digit_display_2 (.value(register_2_q[27:24]));  // open: dp
  Hex_Digit_Display hex_digit_display_3 (.value(register_2_q[23:20]));  // open: dp
  toAlu toalu_1 (
    .v0(main_1_reg1), .a0(main_1_reg2_2), .AluSrc(ALUSrc), .shamt(shamt), .I_imm(I_imm), .X(toalu_1_x),
    .Y(toalu_1_y), .Shamt_Sign(Shamt_Sign), .srav(srav), .bgez(bgez));
  Hex_Digit_Display hex_digit_display_4 (.value(register_2_q[15:12]));  // open: dp
  Hex_Digit_Display hex_digit_display_5 (.value(register_2_q[19:16]));  // open: dp
  // Probe on id_ex_1_pc_2
  // Probe on IRtoBP
  ID_EX id_ex_1 (
    .PC(if_id_1_pc_2), .RegDst(if_id_1_regdst), .ALUop(if_id_1_aluop), .RegWrite(if_id_1_regwrite),
    .IR(if_id_1_ir_2), .MemRead(if_id_1_memread), .MemWrite(if_id_1_memwrite), .I_imm(I_imm),
    .MemtoReg(if_id_1_memtoreg), .addr(if_id_1_out_20), .beq(if_id_1_beq), .bne(if_id_1_bne), .j(if_id_1_j),
    .jal(if_id_1_jal), .jr(if_id_1_jr), .bgez(bgez), .PC_2(id_ex_1_pc_2), .RegDst_2(id_ex_1_regdst_2),
    .ALUop_2(ALUop), .RegWrite_2(id_ex_1_regwrite_2), .IR_2(IRtoBP), .MemRead_2(id_ex_1_memread_2),
    .MemWrite_2(id_ex_1_memwrite_2), .out_33(id_ex_1_out_33), .MemtoReg_2(id_ex_1_memtoreg_2),
    .out_35(id_ex_1_out_35), .beq_2(id_ex_1_beq_2), .bne_2(id_ex_1_bne_2), .j_2(id_ex_1_j_2),
    .jal_2(id_ex_1_jal_2), .jr_2(id_ex_1_jr_2), .bgez_2(id_ex_1_bgez_2), .clk(clk), .x(toalu_1_x),
    .y(toalu_1_y), .out_39(id_ex_1_out_39), .out_42(id_ex_1_out_42), .Din(main_1_reg2_2),
    .Din_2(id_ex_1_din_2), .sb(if_id_1_sb), .sb_2(id_ex_1_sb_2), .v0(main_1_reg1), .v0_2(id_ex_1_v0_2),
    .halt(register_1_q), .halt_2(id_ex_1_halt_2), .reset(reset));
  // Probe on id_ex_1_out_39
  // Probe on id_ex_1_out_42
  Hex_Digit_Display hex_digit_display_6 (.value(register_2_q[11:8]));  // open: dp
  Hex_Digit_Display hex_digit_display_7 (.value(register_2_q[7:4]));  // open: dp
  Hex_Digit_Display hex_digit_display_8 (.value(register_2_q[3:0]));  // open: dp
  ALU alu_1 (
    .AluOP(ALUop), .X(id_ex_1_out_39), .Equal(alu_1_equal), .Result(alu_1_result), .Y(id_ex_1_out_42));  // open: Signed_Overflow, Result_2, UnSigned_Overflow
  bypassing bypassing_1 (.IR(IRtoBP), .clk(clk));  // open: bbrt, brt, bbrs, brs, bbRD, bRD, bbRW, bRW
  Clock clock_1 (.out(clock_1_out));
  // Probe on ALUop
  EX_MEM ex_mem_1 (
    .PC(id_ex_1_pc_2), .RegDst(id_ex_1_regdst_2), .RegWrite(id_ex_1_regwrite_2), .sb(id_ex_1_sb_2),
    .IR(IRtoBP), .MemRead(id_ex_1_memread_2), .MemWrite(id_ex_1_memwrite_2), .I_imm(id_ex_1_out_33),
    .MemtoReg(id_ex_1_memtoreg_2), .addr(id_ex_1_out_35), .beq(id_ex_1_beq_2), .bne(id_ex_1_bne_2),
    .j(id_ex_1_j_2), .jal(id_ex_1_jal_2), .jr(id_ex_1_jr_2), .bgez(id_ex_1_bgez_2), .Din(id_ex_1_din_2),
    .v0(id_ex_1_v0_2), .PC_2(PC), .RegDst_2(RegDst), .RegWrite_2(RegWrite), .sb_2(sb), .IR_2(IR),
    .MemRead_2(MemRead), .MemWrite_2(MemWrite), .I_imm_2(ex_mem_1_i_imm_2), .MemtoReg_2(MemtoReg),
    .addr_2(ex_mem_1_addr_2), .beq_2(beq), .bne_2(bne), .j_2(j), .jal_2(jal), .jr_2(jr), .bgez_2(bgez),
    .Din_2(Din), .v0_2(v0), .clk(clk), .Result(alu_1_result), .Result_2(ex_mem_1_result_2),
    .equal(alu_1_equal), .equal_2(equal), .halt(id_ex_1_halt_2), .halt_2(halt), .reset(reset));
  Counter #(.width(32), .max('hffffffff)) IC (.Q(IC_q), .clk(clk));  // open: load, D, count, carry, clr
  and and_1 (clk, clock_1_out, ~mem_wb_1_halt_2);  // AND_Gate
  // Probe on IC_q
  assign bit_extender_1_out = {{3{1'b0}}, ex_mem_1_result_2[1:0]};  // Bit_Extender bit_extender_1
  Multiplier #(.width(5)) multiplier_1 (
    .a(bit_extender_1_out), .b(5'b01000), .out(multiplier_1_out));  // open: cin, cout
  Demultiplexer #(.select(2), .enable("false")) demultiplexer_1 (
    .out0(demultiplexer_1_out0), .out1(demultiplexer_1_out1), .out2(demultiplexer_1_out2),
    .out3(demultiplexer_1_out3), .in(1'b1), .sel(ex_mem_1_result_2[1:0]));
  branch branch_1 (
    .PC(PC), .beq(beq), .addr(ex_mem_1_addr_2), .equal(equal), .bne(bne), .I_imm(ex_mem_1_i_imm_2), .v0(v0),
    .branch_PC(branch_1_branch_pc), .branch(reset), .bgez(bgez), .bgez_2(ex_mem_1_result_2[0]), .j(j),
    .jal(jal), .jr(jr));
  Multiplexer #(.width(32), .enable("false")) multiplexer_5 (
    .in0(Din), .in1(shifter_1_out), .out(multiplexer_5_out), .sel(sb));
  Shifter #(.width(32)) shifter_1 (.in(Din), .\dist (multiplier_1_out), .out(shifter_1_out));
  or or_1 (or_1_out, ~sb, demultiplexer_1_out0);  // OR_Gate
  or or_2 (or_2_out, ~sb, demultiplexer_1_out1);  // OR_Gate
  or or_3 (or_3_out, ~sb, demultiplexer_1_out2);  // OR_Gate
  or or_4 (or_4_out, ~sb, demultiplexer_1_out3);  // OR_Gate
  RAM #(.addrWidth(10), .bus("separate")) ram_1 (
    .addr(ex_mem_1_result_2[11:2]), .din(multiplexer_5_out[7:0]), .data(ram_1_data), .str(MemWrite),
    .sel(or_1_out), .clk(clk), .ld(MemRead));  // open: clr
  RAM #(.addrWidth(10), .bus("separate")) ram_2 (
    .addr(ex_mem_1_result_2[11:2]), .din(multiplexer_5_out[15:8]), .data(ram_2_data), .str(MemWrite),
    .sel(or_2_out), .clk(clk), .ld(MemRead));  // open: clr
  RAM #(.addrWidth(10), .bus("separate")) ram_3 (
    .addr(ex_mem_1_result_2[11:2]), .din(multiplexer_5_out[23:16]), .data(ram_3_data), .str(MemWrite),
    .sel(or_3_out), .clk(clk), .ld(MemRead));  // open: clr
  RAM #(.addrWidth(10), .bus("separate")) ram_4 (
    .addr(ex_mem_1_result_2[11:2]), .din(multiplexer_5_out[31:24]), .data(ram_4_data), .str(MemWrite),
    .sel(or_4_out), .clk(clk), .ld(MemRead));  // open: clr
  // Probe on PC
  // Probe on IR
  // Probe on mem_wb_1_pc_2
  // Probe on mem_wb_1_ir_2
  Multiplexer #(.width(32), .enable("false")) multiplexer_6 (
    .in0(ex_mem_1_result_2), .in1({ram_4_data, ram_3_data, ram_2_data, ram_1_data}), .out(multiplexer_6_out),
    .sel(MemtoReg));
  MEM_WB mem_wb_1 (
    .RegDst(RegDst), .RegWrite(RegWrite), .PC(PC), .IR(IR), .Din(multiplexer_6_out),
    .RegWrite_2(mem_wb_1_regwrite_2), .PC_2(mem_wb_1_pc_2), .IR_2(mem_wb_1_ir_2), .Din_2(mem_wb_1_din_2),
    .clk(clk), .RW(mem_wb_1_rw), .jal(jal), .halt(halt), .halt_2(mem_wb_1_halt_2));

  // Notes on the sheet:
  //   contents of rom_1 (hex, n*v repeats v):
  //   20110001 8000c05 20110001 20120002 20130003 8000c09 20110001 20120002 20130003 8000c0d 20110001
  //   20120002 20130003 8000c11 20110001 20120002 20130003 c000c14 2002000a c 20100000 22100001 102020
  //   20020022 c 22100002 102020 20020022 c 22100003 102020 20020022 c 22100004 102020 20020022 c 22100005
  //   102020 20020022 c 22100006 102020 20020022 c 22100007 102020 20020022 c 22100008 102020 20020022
  //   20020022 c 3e00008
endmodule

module IF_ID (
  input  [31:0] PC,
  input  [31:0] IR,
  input  reset,
  input  clk,
  output [31:0] PC_2,
  output RegDst,
  output [3:0] ALUop,
  output RegWrite,
  output [31:0] IR_2,
  output Shamt_Sign,
  output MemRead,
  output MemWrite,
  output MemtoReg,
  output ALUSrc,
  output [4:0] out_15,
  output beq,
  output [31:0] out_17,
  output bne,
  output j,
  output [25:0] out_20,
  output jal,
  output systemcall,
  output jr,
  output [4:0] out_24,
  output srav,
  output [4:0] out_26,
  output [4:0] out_27,
  output bgez,
  output sb
);

  wire comparator_1_eq, comparator_2_eq, Sign;
  wire [5:0] decoder_1_func, decoder_1_op;
  wire [15:0] imme;
  wire [31:0] bit_extender_1_out, bit_extender_2_out, multiplexer_2_out;

  Multiplexer #(.width(32), .enable("false")) multiplexer_1 (.in0(PC), .in1({32{1'b0}}), .sel(reset));  // open: out
  Multiplexer #(.width(32), .enable("false")) multiplexer_2 (
    .in0(IR), .in1({32{1'b0}}), .out(multiplexer_2_out), .sel(reset));
  Register #(.width(32)) register_1 (.Q(PC_2), .clk(clk));  // open: D, en, clr
  Register #(.width(32)) register_2 (.D(multiplexer_2_out), .Q(IR_2), .clk(clk));  // open: en, clr
  Decoder decoder_1 (
    .instruction(IR_2), .func(decoder_1_func), .shamt(out_15), .rd(out_27), .rt(out_26), .rs(out_24),
    .op(decoder_1_op), .I_imed(imme), .J_imed(out_20));  // open: mfc0, mtc0, eret
  Control_Unit control_unit_1 (
    .op(decoder_1_op), .funct(decoder_1_func), .RegDst(RegDst), .ALUop(ALUop), .RegWrite(RegWrite),
    .Sign(Sign), .Shamt_Sign(Shamt_Sign), .MemRead(MemRead), .MemWrite(MemWrite), .MemtoReg(MemtoReg),
    .ALUSrc(ALUSrc), .beq(beq), .bne(bne), .j(j), .jal(jal), .jr(jr), .srav(srav), .bgez(bgez), .sb(sb));
  Comparator #(.width(6)) comparator_1 (.a(decoder_1_op), .b({6{1'b0}}), .eq(comparator_1_eq));  // open: gt, lt
  and and_1 (systemcall, comparator_1_eq, comparator_2_eq);
  Comparator #(.width(6)) comparator_2 (.a(decoder_1_func), .b(6'b001100), .eq(comparator_2_eq));  // open: gt, lt
  assign bit_extender_1_out = {{16{1'b0}}, imme};  // Bit_Extender bit_extender_1
  Multiplexer #(.width(32), .enable("false")) multiplexer_3 (
    .in0(bit_extender_1_out), .in1(bit_extender_2_out), .out(out_17), .sel(Sign));
  assign bit_extender_2_out = {{16{imme[15]}}, imme};  // Bit_Extender bit_extender_2

  // Other names for the same wires on the sheet: addr[25:0] = out_20; I_imm[31:0] = out_17; rd[4:0] = out_27;
  //   rs[4:0] = out_24; rt[4:0] = out_26; shamt[4:0] = out_15
endmodule

module ID_EX (
  input  [31:0] PC,
  input  RegDst,
  input  [3:0] ALUop,
  input  RegWrite,
  input  [31:0] IR,
  input  sb,
  input  MemRead,
  input  MemWrite,
  input  [31:0] I_imm,
  input  MemtoReg,
  input  [25:0] addr,
  input  beq,
  input  bne,
  input  j,
  input  [31:0] x,
  input  jal,
  input  jr,
  input  [31:0] y,
  input  bgez,
  input  halt,
  input  [31:0] Din,
  input  [31:0] v0,
  input  clk,
  input  reset,
  output [31:0] PC_2,
  output RegDst_2,
  output [3:0] ALUop_2,
  output RegWrite_2,
  output [31:0] IR_2,
  output sb_2,
  output MemRead_2,
  output MemWrite_2,
  output [31:0] out_33,
  output MemtoReg_2,
  output [25:0] out_35,
  output beq_2,
  output bne_2,
  output j_2,
  output [31:0] out_39,
  output jal_2,
  output jr_2,
  output [31:0] out_42,
  output bgez_2,
  output halt_2,
  output [31:0] Din_2,
  output [31:0] v0_2
);

  wire [16:0] multiplexer_9_out;
  wire [25:0] multiplexer_4_out;
  wire [31:0] multiplexer_1_out, multiplexer_2_out, multiplexer_3_out, multiplexer_5_out, multiplexer_6_out,
       multiplexer_7_out, multiplexer_8_out;

  Multiplexer #(.width(32), .enable("false")) multiplexer_1 (
    .in0(PC), .in1({32{1'b0}}), .out(multiplexer_1_out), .sel(reset));
  Multiplexer #(.width(32), .enable("false")) multiplexer_2 (
    .in0(IR), .in1({32{1'b0}}), .out(multiplexer_2_out), .sel(reset));
  Multiplexer #(.width(32), .enable("false")) multiplexer_3 (
    .in0(I_imm), .in1({32{1'b0}}), .out(multiplexer_3_out), .sel(reset));
  Multiplexer #(.width(26), .enable("false")) multiplexer_4 (
    .in0(addr), .in1({26{1'b0}}), .out(multiplexer_4_out), .sel(reset));
  Multiplexer #(.width(32), .enable("false")) multiplexer_5 (
    .in0(x), .in1({32{1'b0}}), .out(multiplexer_5_out), .sel(reset));
  Multiplexer #(.width(32), .enable("false")) multiplexer_6 (
    .in0(y), .in1({32{1'b0}}), .out(multiplexer_6_out), .sel(reset));
  Multiplexer #(.width(32), .enable("false")) multiplexer_7 (
    .in0(Din), .in1({32{1'b0}}), .out(multiplexer_7_out), .sel(reset));
  Multiplexer #(.width(32), .enable("false")) multiplexer_8 (
    .in0(v0), .in1({32{1'b0}}), .out(multiplexer_8_out), .sel(reset));
  Register #(.width(32)) register_1 (.D(multiplexer_1_out), .Q(PC_2), .clk(clk));  // open: en, clr
  Register #(.width(32)) register_2 (.D(multiplexer_2_out), .Q(IR_2), .clk(clk));  // open: en, clr
  Register #(.width(32)) register_3 (.D(multiplexer_3_out), .Q(out_33), .clk(clk));  // open: en, clr
  Register #(.width(26)) register_4 (.D(multiplexer_4_out), .Q(out_35), .clk(clk));  // open: en, clr
  Register #(.width(32)) register_5 (.D(multiplexer_5_out), .Q(out_39), .clk(clk));  // open: en, clr
  Register #(.width(32)) register_6 (.D(multiplexer_6_out), .Q(out_42), .clk(clk));  // open: en, clr
  Register #(.width(32)) register_7 (.D(multiplexer_7_out), .Q(Din_2), .clk(clk));  // open: en, clr
  Register #(.width(32)) register_8 (.D(multiplexer_8_out), .Q(v0_2), .clk(clk));  // open: en, clr
  Multiplexer #(.width(17), .enable("false")) multiplexer_9 (
    .in0({halt, bgez, jr, jal, j, bne, beq, MemtoReg, MemWrite, MemRead, sb, RegWrite, ALUop, RegDst}),
    .in1({17{1'b0}}), .out(multiplexer_9_out), .sel(reset));
  Register #(.width(17)) register_9 (
    .D(multiplexer_9_out),
    .Q({halt_2, bgez_2, jr_2, jal_2, j_2, bne_2, beq_2, MemtoReg_2, MemWrite_2, MemRead_2, sb_2, RegWrite_2, ALUop_2, RegDst_2}),
    .clk(clk));  // open: en, clr
endmodule

module EX_MEM (
  input  [31:0] PC,
  input  RegDst,
  input  RegWrite,
  input  [31:0] IR,
  input  sb,
  input  MemRead,
  input  MemWrite,
  input  [31:0] I_imm,
  input  MemtoReg,
  input  equal,
  input  [25:0] addr,
  input  beq,
  input  bne,
  input  j,
  input  [31:0] Din,
  input  jal,
  input  jr,
  input  [31:0] v0,
  input  bgez,
  input  halt,
  input  [31:0] Result,
  input  clk,
  input  reset,
  output [31:0] PC_2,
  output RegDst_2,
  output RegWrite_2,
  output [31:0] IR_2,
  output sb_2,
  output MemRead_2,
  output MemWrite_2,
  output [31:0] I_imm_2,
  output MemtoReg_2,
  output equal_2,
  output [25:0] addr_2,
  output beq_2,
  output bne_2,
  output j_2,
  output [31:0] Din_2,
  output jal_2,
  output jr_2,
  output [31:0] v0_2,
  output bgez_2,
  output halt_2,
  output [31:0] Result_2
);

  wire [13:0] multiplexer_8_out;
  wire [25:0] multiplexer_4_out;
  wire [31:0] multiplexer_1_out, multiplexer_2_out, multiplexer_3_out, multiplexer_5_out, multiplexer_6_out,
       multiplexer_7_out;

  Multiplexer #(.width(32), .enable("false")) multiplexer_1 (
    .in0(PC), .in1({32{1'b0}}), .out(multiplexer_1_out), .sel(reset));
  Multiplexer #(.width(32), .enable("false")) multiplexer_2 (
    .in0(IR), .in1({32{1'b0}}), .out(multiplexer_2_out), .sel(reset));
  Multiplexer #(.width(32), .enable("false")) multiplexer_3 (
    .in0(I_imm), .in1({32{1'b0}}), .out(multiplexer_3_out), .sel(reset));
  Multiplexer #(.width(26), .enable("false")) multiplexer_4 (
    .in0(addr), .in1({26{1'b0}}), .out(multiplexer_4_out), .sel(reset));
  Multiplexer #(.width(32), .enable("false")) multiplexer_5 (
    .in0(Din), .in1({32{1'b0}}), .out(multiplexer_5_out), .sel(reset));
  Multiplexer #(.width(32), .enable("false")) multiplexer_6 (
    .in0(v0), .in1({32{1'b0}}), .out(multiplexer_6_out), .sel(reset));
  Multiplexer #(.width(32), .enable("false")) multiplexer_7 (
    .in0(Result), .in1({32{1'b0}}), .out(multiplexer_7_out), .sel(reset));
  Register #(.width(32)) register_1 (.D(multiplexer_1_out), .Q(PC_2), .clk(clk));  // open: en, clr
  Register #(.width(32)) register_2 (.D(multiplexer_2_out), .Q(IR_2), .clk(clk));  // open: en, clr
  Register #(.width(32)) register_3 (.D(multiplexer_3_out), .Q(I_imm_2), .clk(clk));  // open: en, clr
  Register #(.width(26)) register_4 (.D(multiplexer_4_out), .Q(addr_2), .clk(clk));  // open: en, clr
  Register #(.width(32)) register_5 (.D(multiplexer_5_out), .Q(Din_2), .clk(clk));  // open: en, clr
  Register #(.width(32)) register_6 (.D(multiplexer_6_out), .Q(v0_2), .clk(clk));  // open: en, clr
  Register #(.width(32)) register_7 (.D(multiplexer_7_out), .Q(Result_2), .clk(clk));  // open: en, clr
  Multiplexer #(.width(14), .enable("false")) multiplexer_8 (
    .in0({halt, bgez, jr, jal, j, bne, beq, equal, MemtoReg, MemWrite, MemRead, sb, RegWrite, RegDst}),
    .in1({14{1'b0}}), .out(multiplexer_8_out), .sel(reset));
  Register #(.width(14)) register_8 (
    .D(multiplexer_8_out),
    .Q({halt_2, bgez_2, jr_2, jal_2, j_2, bne_2, beq_2, equal_2, MemtoReg_2, MemWrite_2, MemRead_2, sb_2, RegWrite_2, RegDst_2}),
    .clk(clk));  // open: en, clr
endmodule

module MEM_WB (
  input  halt,
  input  [31:0] PC,
  input  RegWrite,
  input  [31:0] IR,
  input  [31:0] Din,
  input  clk,
  input  jal,
  input  RegDst,
  output halt_2,
  output [31:0] PC_2,
  output RegWrite_2,
  output [31:0] IR_2,
  output [31:0] Din_2,
  output [4:0] RW
);

  wire [4:0] multiplexer_2_out, multiplexer_3_out;
  wire [31:0] adder_1_out, multiplexer_1_out;

  Adder #(.width(32)) adder_1 (.a(PC), .b(32'h4), .out(adder_1_out));  // open: cin, cout
  Multiplexer #(.width(32), .enable("false")) multiplexer_1 (
    .in0(Din), .in1(adder_1_out), .out(multiplexer_1_out), .sel(jal));
  Register #(.width(32)) register_1 (.D(PC), .Q(PC_2), .clk(clk));  // open: en, clr
  Register #(.width(32)) register_2 (.D(IR), .Q(IR_2), .clk(clk));  // open: en, clr
  Register #(.width(32)) register_3 (.D(multiplexer_1_out), .Q(Din_2), .clk(clk));  // open: en, clr
  Multiplexer #(.width(5), .enable("false")) multiplexer_2 (
    .in0(IR[20:16]), .in1(IR[15:11]), .out(multiplexer_2_out), .sel(RegDst));
  Multiplexer #(.width(5), .enable("false")) multiplexer_3 (
    .in0(multiplexer_2_out), .in1({5{1'b1}}), .out(multiplexer_3_out), .sel(jal));
  Register #(.width(5)) register_4 (.D(multiplexer_3_out), .Q(RW), .clk(clk));  // open: en, clr
  Register #(.width(1)) register_5 (.D(halt), .Q(halt_2), .clk(clk));  // open: en, clr
  Register #(.width(1)) register_6 (.D(RegWrite), .Q(RegWrite_2), .clk(clk));  // open: en, clr
endmodule

module Control_Unit (
  input  [5:0] op,
  input  [5:0] funct,
  output RegDst,
  output [3:0] ALUop,
  output RegWrite,
  output Sign,
  output Shamt_Sign,
  output MemRead,
  output MemWrite,
  output MemtoReg,
  output ALUSrc,
  output beq,
  output bne,
  output j,
  output jal,
  output jr,
  output srav,
  output bgez,
  output sb
);

  wire add, addi, addiu, addu, \and , andi, \nor , \or , ori, sll, slt, slti, sltiu, sltu, sra, srl, sub, sw;

  I_type i_type_1 (
    .op5(op[5]), .op4(op[4]), .op3(op[3]), .op2(op[2]), .op1(op[1]), .op0(op[0]), .addi(addi), .addiu(addiu),
    .andi(andi), .ori(ori), .lw(MemtoReg), .sw(sw), .beq(beq), .bne(bne), .slti(slti), .j(j), .jal(jal),
    .fenable(RegDst), .sltiu(sltiu), .sb(sb), .bgez(bgez));
  R_type r_type_1 (
    .fenable(RegDst), .funct5(funct[5]), .funct4(funct[4]), .funct3(funct[3]), .funct2(funct[2]),
    .funct1(funct[1]), .funct0(funct[0]), .add(add), .addu(addu), .\and (\and ), .sll(sll), .sra(sra),
    .srl(srl), .sub(sub), .\or (\or ), .\nor (\nor ), .slt(slt), .sltu(sltu), .jr(jr), .srav(srav));
  or or_1 (RegWrite, sltiu, add, addu, \and , sll, sra, srl, sub, \or , \nor , sltu, addi, addiu, andi, ori, MemtoReg, slti, slt, jal, srav);
  or or_2 (Sign, sb, addi, MemtoReg, sw, beq, bne, slti, bgez);
  or or_3 (Shamt_Sign, sll, sra, srav, srl);
  or or_4 (ALUSrc, sltiu, addi, addiu, andi, ori, MemtoReg, sw, slti, sb);
  or or_5 (ALUop[3], sltiu, \or , ori, \nor , slt, slti, sltu, bgez);
  or or_6 (ALUop[2], sltiu, add, addi, addu, addiu, \and , sub, andi, MemtoReg, sw, sltu, sb);
  or or_7 (ALUop[1], bgez, andi, sub, \nor , slt, slti, srl, \and );
  or or_8 (ALUop[0], bgez, srav, addi, addu, addiu, \and , andi, sra, slti, MemtoReg, sw, slt, add, sb);
  or or_9 (MemRead, MemtoReg, sb);
  or or_10 (MemWrite, sb, sw);

  // Other names for the same wires on the sheet: lw = MemtoReg
endmodule

module Decoder (
  input  [31:0] instruction,
  output mfc0,
  output [5:0] func,
  output [4:0] shamt,
  output [4:0] rd,
  output mtc0,
  output [4:0] rt,
  output [4:0] rs,
  output [5:0] op,
  output [15:0] I_imed,
  output [25:0] J_imed,
  output eret
);

  wire comparator_1_eq, comparator_2_eq, comparator_3_eq;

  Comparator #(.width(5)) comparator_1 (.a(instruction[25:21]), .b({5{1'b0}}), .eq(comparator_1_eq));  // open: gt, lt
  Comparator #(.width(5)) comparator_2 (.a(instruction[25:21]), .b(5'b00100), .eq(comparator_2_eq));  // open: gt, lt
  Comparator #(.width(6)) comparator_3 (.a(instruction[31:26]), .b(6'b010000), .eq(comparator_3_eq));  // open: gt, lt
  Comparator #(.width(32)) comparator_4 (.a(32'h42000018), .b(instruction), .eq(eret));  // open: gt, lt
  and and_1 (mfc0, comparator_1_eq, comparator_3_eq);
  and and_2 (mtc0, comparator_2_eq, comparator_3_eq);

  assign func = instruction[5:0];
  assign I_imed = instruction[15:0];
  assign J_imed = instruction[25:0];
  assign op = instruction[31:26];
  assign rd = instruction[15:11];
  assign rs = instruction[25:21];
  assign rt = instruction[20:16];
  assign shamt = instruction[10:6];
endmodule

module I_type (
  input  op5,
  input  op4,
  input  op3,
  input  op2,
  input  op1,
  input  op0,
  output addi,
  output addiu,
  output andi,
  output ori,
  output lw,
  output sw,
  output beq,
  output bne,
  output slti,
  output j,
  output jal,
  output sltiu,
  output sb,
  output bgez,
  output fenable
);

  wire not_1_out, not_2_out, not_3_out, not_4_out, not_5_out, not_6_out, not_7_out, not_8_out, not_9_out,
       not_10_out, not_11_out, not_12_out, not_13_out, not_14_out, not_15_out, not_16_out, not_17_out,
       not_18_out, not_19_out, not_20_out, not_21_out, not_22_out, not_23_out, not_24_out, not_25_out,
       not_26_out, not_27_out, not_28_out, not_29_out, not_30_out, not_31_out, not_32_out, not_33_out,
       not_34_out, not_35_out, not_36_out, not_37_out, not_38_out, not_39_out, not_40_out, not_41_out,
       not_42_out, not_43_out, not_44_out, not_45_out, not_46_out, not_47_out, not_48_out, not_49_out,
       not_50_out, not_51_out, not_52_out, not_53_out, not_54_out, not_55_out, not_56_out, not_57_out,
       not_58_out, not_59_out, not_60_out, not_61_out;

  not not_1 (not_1_out, op5);
  not not_2 (not_2_out, op4);
  not not_3 (not_3_out, op2);
  not not_4 (not_4_out, op1);
  not not_5 (not_5_out, op0);
  not not_6 (not_6_out, op5);
  not not_7 (not_7_out, op4);
  not not_8 (not_8_out, op2);
  not not_9 (not_9_out, op1);
  not not_10 (not_10_out, op5);
  not not_11 (not_11_out, op4);
  not not_12 (not_12_out, op1);
  not not_13 (not_13_out, op0);
  not not_14 (not_14_out, op5);
  not not_15 (not_15_out, op4);
  not not_16 (not_16_out, op1);
  not not_17 (not_17_out, op4);
  not not_18 (not_18_out, op3);
  not not_19 (not_19_out, op2);
  not not_20 (not_20_out, op4);
  not not_21 (not_21_out, op2);
  not not_22 (not_22_out, op5);
  not not_23 (not_23_out, op4);
  not not_24 (not_24_out, op3);
  not not_25 (not_25_out, op1);
  not not_26 (not_26_out, op0);
  not not_27 (not_27_out, op5);
  not not_28 (not_28_out, op4);
  not not_29 (not_29_out, op3);
  not not_30 (not_30_out, op1);
  not not_31 (not_31_out, op5);
  not not_32 (not_32_out, op4);
  not not_33 (not_33_out, op2);
  not not_34 (not_34_out, op0);
  not not_35 (not_35_out, op5);
  not not_36 (not_36_out, op4);
  not not_37 (not_37_out, op3);
  not not_38 (not_38_out, op2);
  not not_39 (not_39_out, op0);
  not not_40 (not_40_out, op5);
  not not_41 (not_41_out, op4);
  not not_42 (not_42_out, op3);
  not not_43 (not_43_out, op2);
  not not_44 (not_44_out, op5);
  not not_45 (not_45_out, op4);
  not not_46 (not_46_out, op2);
  not not_47 (not_47_out, op4);
  not not_48 (not_48_out, op2);
  not not_49 (not_49_out, op1);
  not not_50 (not_50_out, op0);
  not not_51 (not_51_out, op5);
  not not_52 (not_52_out, op4);
  not not_53 (not_53_out, op3);
  not not_54 (not_54_out, op2);
  not not_55 (not_55_out, op1);
  not not_56 (not_56_out, op5);
  not not_57 (not_57_out, op4);
  not not_58 (not_58_out, op3);
  not not_59 (not_59_out, op2);
  not not_60 (not_60_out, op1);
  not not_61 (not_61_out, op0);
  and and_1 (addi, not_1_out, not_2_out, op3, not_3_out, not_4_out, not_5_out);
  and and_2 (addiu, not_6_out, not_7_out, op3, not_8_out, not_9_out, op0);
  and and_3 (andi, not_10_out, not_11_out, op3, op2, not_12_out, not_13_out);
  and and_4 (ori, not_14_out, not_15_out, op3, op2, not_16_out, op0);
  and and_5 (lw, op5, not_17_out, not_18_out, not_19_out, op1, op0);
  and and_6 (sw, op5, not_20_out, op3, not_21_out, op1, op0);
  and and_7 (beq, not_22_out, not_23_out, not_24_out, op2, not_25_out, not_26_out);
  and and_8 (bne, not_27_out, not_28_out, not_29_out, op2, not_30_out, op0);
  and and_9 (slti, not_31_out, not_32_out, op3, not_33_out, op1, not_34_out);
  and and_10 (j, not_35_out, not_36_out, not_37_out, not_38_out, op1, not_39_out);
  and and_11 (jal, not_40_out, not_41_out, not_42_out, not_43_out, op1, op0);
  and and_12 (sltiu, not_44_out, not_45_out, op3, not_46_out, op1, op0);
  and and_13 (sb, op5, not_47_out, op3, not_48_out, not_49_out, not_50_out);
  and and_14 (bgez, not_51_out, not_52_out, not_53_out, not_54_out, not_55_out, op0);
  and and_15 (fenable, not_56_out, not_57_out, not_58_out, not_59_out, not_60_out, not_61_out);
endmodule

module R_type (
  input  fenable,
  input  funct5,
  input  funct4,
  input  funct3,
  input  funct2,
  input  funct1,
  input  funct0,
  output add,
  output addu,
  output \and ,
  output sll,
  output sra,
  output srl,
  output sub,
  output \or ,
  output \nor ,
  output slt,
  output sltu,
  output jr,
  output srav
);

  wire and_1_out, and_2_out, and_3_out, and_4_out, and_5_out, and_6_out, and_7_out, and_8_out, and_9_out,
       and_10_out, and_11_out, and_12_out, and_13_out, not_1_out, not_2_out, not_3_out, not_4_out, not_5_out,
       not_6_out, not_7_out, not_8_out, not_9_out, not_10_out, not_11_out, not_12_out, not_13_out,
       not_14_out, not_15_out, not_16_out, not_17_out, not_18_out, not_19_out, not_20_out, not_21_out,
       not_22_out, not_23_out, not_24_out, not_25_out, not_26_out, not_27_out, not_28_out, not_29_out,
       not_30_out, not_31_out, not_32_out, not_33_out, not_34_out, not_35_out, not_36_out, not_37_out,
       not_38_out, not_39_out, not_40_out, not_41_out, not_42_out, not_43_out, not_44_out, not_45_out,
       not_46_out, not_47_out, not_48_out, not_49_out, not_50_out;

  not not_1 (not_1_out, funct4);
  not not_2 (not_2_out, funct3);
  not not_3 (not_3_out, funct2);
  not not_4 (not_4_out, funct1);
  not not_5 (not_5_out, funct0);
  not not_6 (not_6_out, funct4);
  not not_7 (not_7_out, funct3);
  not not_8 (not_8_out, funct2);
  not not_9 (not_9_out, funct1);
  not not_10 (not_10_out, funct4);
  not not_11 (not_11_out, funct3);
  not not_12 (not_12_out, funct1);
  not not_13 (not_13_out, funct0);
  not not_14 (not_14_out, funct5);
  not not_15 (not_15_out, funct4);
  not not_16 (not_16_out, funct3);
  not not_17 (not_17_out, funct2);
  not not_18 (not_18_out, funct1);
  not not_19 (not_19_out, funct0);
  not not_20 (not_20_out, funct5);
  not not_21 (not_21_out, funct4);
  not not_22 (not_22_out, funct3);
  not not_23 (not_23_out, funct2);
  not not_24 (not_24_out, funct5);
  not not_25 (not_25_out, funct4);
  not not_26 (not_26_out, funct3);
  not not_27 (not_27_out, funct2);
  not not_28 (not_28_out, funct0);
  not not_29 (not_29_out, funct4);
  not not_30 (not_30_out, funct3);
  not not_31 (not_31_out, funct2);
  not not_32 (not_32_out, funct0);
  not not_33 (not_33_out, funct4);
  not not_34 (not_34_out, funct3);
  not not_35 (not_35_out, funct1);
  not not_36 (not_36_out, funct4);
  not not_37 (not_37_out, funct3);
  not not_38 (not_38_out, funct4);
  not not_39 (not_39_out, funct2);
  not not_40 (not_40_out, funct0);
  not not_41 (not_41_out, funct4);
  not not_42 (not_42_out, funct2);
  not not_43 (not_43_out, funct5);
  not not_44 (not_44_out, funct4);
  not not_45 (not_45_out, funct2);
  not not_46 (not_46_out, funct1);
  not not_47 (not_47_out, funct0);
  not not_48 (not_48_out, funct5);
  not not_49 (not_49_out, funct4);
  not not_50 (not_50_out, funct3);
  and and_1 (and_1_out, funct5, not_1_out, not_2_out, not_3_out, not_4_out, not_5_out);
  and and_2 (and_2_out, funct5, not_6_out, not_7_out, not_8_out, not_9_out, funct0);
  and and_3 (and_3_out, funct5, not_10_out, not_11_out, funct2, not_12_out, not_13_out);
  and and_4 (and_4_out, not_14_out, not_15_out, not_16_out, not_17_out, not_18_out, not_19_out);
  and and_5 (and_5_out, not_20_out, not_21_out, not_22_out, not_23_out, funct1, funct0);
  and and_6 (and_6_out, not_24_out, not_25_out, not_26_out, not_27_out, funct1, not_28_out);
  and and_7 (and_7_out, funct5, not_29_out, not_30_out, not_31_out, funct1, not_32_out);
  and and_8 (and_8_out, funct5, not_33_out, not_34_out, funct2, not_35_out, funct0);
  and and_9 (and_9_out, funct5, not_36_out, not_37_out, funct2, funct1, funct0);
  and and_10 (and_10_out, funct5, not_38_out, funct3, not_39_out, funct1, not_40_out);
  and and_11 (and_11_out, funct5, not_41_out, funct3, not_42_out, funct1, funct0);
  and and_12 (and_12_out, not_43_out, not_44_out, funct3, not_45_out, not_46_out, not_47_out);
  and and_13 (and_13_out, not_48_out, not_49_out, not_50_out, funct2, funct1, funct0);
  and and_14 (add, fenable, and_1_out);
  and and_15 (addu, fenable, and_2_out);
  and and_16 (\and , fenable, and_3_out);
  and and_17 (sll, fenable, and_4_out);
  and and_18 (sra, fenable, and_5_out);
  and and_19 (srl, fenable, and_6_out);
  and and_20 (sub, fenable, and_7_out);
  and and_21 (\or , fenable, and_8_out);
  and and_22 (\nor , fenable, and_9_out);
  and and_23 (slt, fenable, and_10_out);
  and and_24 (sltu, fenable, and_11_out);
  and and_25 (jr, fenable, and_12_out);
  and and_26 (srav, fenable, and_13_out);
endmodule

module toAlu (
  input  [31:0] v0,
  input  [31:0] a0,
  input  AluSrc,
  input  srav,
  input  bgez,
  input  [4:0] shamt,
  input  [31:0] I_imm,
  input  Shamt_Sign,
  output [31:0] X,
  output [31:0] Y
);

  wire [31:0] and_1_out, bit_extender_1_out, multiplexer_1_out, multiplexer_3_out, multiplexer_4_out;

  Multiplexer #(.width(32), .enable("false")) multiplexer_1 (
    .in0(a0), .in1(I_imm), .out(multiplexer_1_out), .sel(AluSrc));
  assign bit_extender_1_out = {{27{1'b0}}, shamt};  // Bit_Extender bit_extender_1
  Multiplexer #(.width(32), .enable("false")) multiplexer_2 (.in0(v0), .in1(a0), .out(X), .sel(Shamt_Sign));
  Multiplexer #(.width(32), .enable("false")) multiplexer_3 (
    .in0(multiplexer_1_out), .in1(bit_extender_1_out), .out(multiplexer_3_out), .sel(Shamt_Sign));
  assign and_1_out = v0 & 32'h1f;  // AND_Gate and_1, 32 bits wide
  Multiplexer #(.width(32), .enable("false")) multiplexer_4 (
    .in0(multiplexer_3_out), .in1(and_1_out), .out(multiplexer_4_out), .sel(srav));
  Multiplexer #(.width(32), .enable("false")) multiplexer_5 (
    .in0(multiplexer_4_out), .in1({32{1'b0}}), .out(Y), .sel(bgez));
endmodule

module branch (
  input  [31:0] PC,
  input  jr,
  input  beq,
  input  j,
  input  [25:0] addr,
  input  equal,
  input  jal,
  input  bne,
  input  [31:0] I_imm,
  input  bgez,
  input  [31:0] v0,
  input  bgez_2,
  output [31:0] branch_PC,
  output branch
);

  wire and_1_out, and_2_out, and_3_out, not_1_out, or_1_out, or_2_out;
  wire [31:0] adder_1_out, adder_2_out, multiplexer_1_out, multiplexer_2_out, shifter_1_out;

  Adder #(.width(32)) adder_1 (.a(PC), .b(32'h4), .out(adder_1_out));  // open: cin, cout
  Shifter #(.width(32)) shifter_1 (.in(I_imm), .\dist (5'b00010), .out(shifter_1_out));
  and and_1 (and_1_out, bgez, not_1_out);
  and and_2 (and_2_out, beq, equal);
  and and_3 (and_3_out, ~equal, bne);  // AND_Gate
  not not_1 (not_1_out, bgez_2);
  Adder #(.width(32)) adder_2 (.a(adder_1_out), .b(shifter_1_out), .out(adder_2_out));  // open: cin, cout
  or or_1 (or_1_out, and_2_out, and_1_out, and_3_out);
  Multiplexer #(.width(32), .enable("false")) multiplexer_1 (
    .in0(adder_1_out), .in1(adder_2_out), .out(multiplexer_1_out), .sel(or_1_out));
  Multiplexer #(.width(32), .enable("false")) multiplexer_2 (
    .in0(multiplexer_1_out), .in1({adder_1_out[31:28], addr, 2'b00}), .out(multiplexer_2_out), .sel(or_2_out));
  or or_2 (or_2_out, j, jal);
  Multiplexer #(.width(32), .enable("false")) multiplexer_3 (
    .in0(multiplexer_2_out), .in1(v0), .out(branch_PC), .sel(jr));
  or or_3 (branch, or_1_out, or_2_out, jr);
endmodule

module bypassing (
  input  [31:0] IR,
  input  bbRD,
  input  bbRW,
  input  bRD,
  input  bRW,
  input  clk,
  output bbrt,
  output brt,
  output bbrs,
  output brs
);

  wire [4:0] multiplexer_1_out, multiplexer_2_out;
  wire [31:0] register_1_q, register_2_q;

  Register #(.width(32)) register_1 (.D(IR), .Q(register_1_q), .clk(clk));  // open: en, clr
  Register #(.width(32)) register_2 (.D(register_1_q), .Q(register_2_q), .clk(clk));  // open: en, clr
  Multiplexer #(.width(5)) multiplexer_1 (
    .in0(register_2_q[20:16]), .in1(register_2_q[15:11]), .out(multiplexer_1_out), .sel(bbRD), .en(bbRW));
  Multiplexer #(.width(5)) multiplexer_2 (
    .in0(register_1_q[20:16]), .in1(register_1_q[15:11]), .out(multiplexer_2_out), .sel(bRD), .en(bRW));
  Comparator #(.width(5)) comparator_1 (.a(multiplexer_1_out), .b(IR[20:16]), .eq(bbrt));  // open: gt, lt
  Comparator #(.width(5)) comparator_2 (.a(multiplexer_2_out), .b(IR[20:16]), .eq(brt));  // open: gt, lt
  Comparator #(.width(5)) comparator_3 (.a(multiplexer_1_out), .b(IR[25:21]), .eq(bbrs));  // open: gt, lt
  Comparator #(.width(5)) comparator_4 (.a(multiplexer_2_out), .b(IR[25:21]), .eq(brs));  // open: gt, lt
endmodule
